// Logisim project ArcosHerreraRaul-P2.circ as structural Verilog: 1 circuit, main circuit main
module main (
  input  in_1,
  input  in_2,
  input  in_3,
  input  Dato,
  input  in_5,
  input  in_6,
  input  in_7,
  input  in_8,
  input  in_9,
  input  in_10,
  input  in_11,
  input  Dato_2,
  input  in_13,
  input  in_14,
  input  in_15,
  input  in_16,
  input  Inicio,
  input  Receptor,
  input  in_19,
  input  Receptor_2,
  input  in_21,
  input  in_22,
  input  in_23,
  input  in_24,
  input  in_25,
  input  Dato_3,
  input  in_27,
  input  in_28,
  input  in_29,
  input  in_30,
  input  in_31,
  input  in_32,
  input  in_33,
  input  Dato_4,
  input  in_35,
  input  in_36,
  input  in_37,
  input  in_38,
  input  in_39,
  input  Receptor_3,
  input  in_41,
  input  Receptor_4,
  input  in_43,
  input  in_44,
  input  in_45,
  output [12:0] out_46,
  output [12:0] out_47,
  output [12:0] out_48,
  output [12:0] out_49
);

  wire and_1_out, and_2_out, and_3_out, and_4_out, and_5_out, and_6_out, clock_1_out,
       controlled_buffer_1_out, decoder_1_out0, decoder_1_out1, decoder_1_out2, decoder_2_out3,
       even_parity_1_out, even_parity_2_out, even_parity_3_out, even_parity_4_out, not_1_out, or_1_out,
       or_2_out, or_3_out, or_4_out, or_5_out, or_6_out, or_7_out, or_8_out, shift_register_1_out,
       shift_register_2_out, shift_register_3_out, shift_register_4_out, undriven;
  wire [3:0] counter_1_q;
  wire [12:0] shift_register_1_q12, shift_register_2_q12, shift_register_3_q12, shift_register_4_q12;

  Shift_Register #(.length(13)) shift_register_1 (
    .shift(or_2_out), .in(controlled_buffer_1_out), .clk(and_4_out), .out(shift_register_1_out),
    .load(Inicio), .d0(Receptor), .q0(shift_register_1_q12[12]), .d1(in_19), .q1(shift_register_1_q12[11]),
    .d2(1'b1), .q2(shift_register_1_q12[10]), .d3(1'b1), .q3(shift_register_1_q12[9]), .d4(in_1),
    .q4(shift_register_1_q12[8]), .d5(in_2), .q5(shift_register_1_q12[7]), .d6(in_3),
    .q6(shift_register_1_q12[6]), .d7(Dato), .q7(shift_register_1_q12[5]), .d8(in_5),
    .q8(shift_register_1_q12[4]), .d9(in_6), .q9(shift_register_1_q12[3]), .d10(in_7),
    .q10(shift_register_1_q12[2]), .d11(in_8), .q11(shift_register_1_q12[1]), .d12(even_parity_1_out),
    .q12(shift_register_1_q12[0]));  // open: clr
  Decoder #(.select(2)) decoder_1 (
    .out0(decoder_1_out0), .out1(decoder_1_out1), .out2(decoder_1_out2), .sel({in_19, Receptor}), .en(in_22));  // open: out3
  Shift_Register #(.length(13)) shift_register_2 (
    .shift(or_4_out), .in(controlled_buffer_1_out), .clk(and_4_out), .out(shift_register_2_out),
    .load(Inicio), .d0(Receptor_3), .q0(shift_register_2_q12[12]), .d1(in_41), .q1(shift_register_2_q12[11]),
    .d2(1'b1), .q2(shift_register_2_q12[10]), .d3(1'b1), .q3(shift_register_2_q12[9]), .d4(in_24),
    .q4(shift_register_2_q12[8]), .d5(in_25), .q5(shift_register_2_q12[7]), .d6(Dato_3),
    .q6(shift_register_2_q12[6]), .d7(in_27), .q7(shift_register_2_q12[5]), .d8(in_28),
    .q8(shift_register_2_q12[4]), .d9(in_29), .q9(shift_register_2_q12[3]), .d10(in_30),
    .q10(shift_register_2_q12[2]), .d11(in_31), .q11(shift_register_2_q12[1]), .d12(undriven),
    .q12(shift_register_2_q12[0]));  // open: clr
  Decoder #(.select(2)) decoder_2 (
    .out0(decoder_1_out0), .out2(decoder_1_out2), .out3(decoder_2_out3), .sel({in_41, Receptor_3}), .en(in_44));  // open: out1
  and and_1 (and_1_out, shift_register_1_q12[12], shift_register_1_q12[11], and_3_out);
  and and_2 (and_2_out, shift_register_2_q12[12], ~shift_register_2_q12[11], and_3_out);  // AND_Gate
  or or_1 (or_1_out, ~Receptor, ~in_19);  // OR_Gate
  or or_2 (or_2_out, or_1_out, decoder_2_out3);
  or or_3 (or_3_out, ~Receptor_3, in_41);  // OR_Gate
  or or_4 (or_4_out, or_3_out, decoder_1_out1);
  assign controlled_buffer_1_out = or_1_out ? shift_register_1_out : 1'bz;  // Controlled_Buffer controlled_buffer_1
  assign controlled_buffer_1_out = or_3_out ? shift_register_2_out : 1'bz;  // Controlled_Buffer controlled_buffer_2
  xnor even_parity_1 (even_parity_1_out, in_1, in_2, in_3, Dato, in_5, in_6, in_7, in_8);
  Hex_Digit_Display hex_digit_display_1 (.value(out_46[12:9]));  // open: dp
  Register #(.width(13)) register_1 (.D(shift_register_1_q12), .Q(out_46), .clk(and_1_out));  // open: en, clr
  xnor even_parity_2 (even_parity_2_out, in_24, in_25, Dato_3, in_27, in_28, in_29, in_30, in_31);
  Hex_Digit_Display hex_digit_display_2 (.value(out_48[12:9]));  // open: dp
  Register #(.width(13)) register_2 (.D(shift_register_2_q12), .Q(out_48), .clk(and_2_out));  // open: en, clr
  Hex_Digit_Display hex_digit_display_3 (.value(out_46[4:1]));  // open: dp
  Hex_Digit_Display hex_digit_display_4 (.value(out_46[8:5]));  // open: dp
  Hex_Digit_Display hex_digit_display_5 (.value(out_48[8:5]));  // open: dp
  Hex_Digit_Display hex_digit_display_6 (.value(out_48[4:1]));  // open: dp
  Hex_Digit_Display hex_digit_display_7 (.value({3'b000, out_46[0]}));  // open: dp
  Hex_Digit_Display hex_digit_display_8 (.value({3'b000, out_48[0]}));  // open: dp
  Counter #(.width(4), .max('hf)) counter_1 (
    .Q(counter_1_q), .clk(and_4_out), .clr(Inicio));  // open: load, D, count, carry
  Clock clock_1 (.out(clock_1_out));
  and and_3 (and_3_out, counter_1_q[3], counter_1_q[2], counter_1_q[0]);
  not not_1 (not_1_out, and_3_out);
  and and_4 (and_4_out, clock_1_out, not_1_out);
  Shift_Register #(.length(13)) shift_register_3 (
    .shift(or_6_out), .in(controlled_buffer_1_out), .clk(and_4_out), .out(shift_register_3_out),
    .load(Inicio), .d0(Receptor_2), .q0(shift_register_3_q12[12]), .d1(in_21), .q1(shift_register_3_q12[11]),
    .d2(1'b0), .q2(shift_register_3_q12[10]), .d3(1'b1), .q3(shift_register_3_q12[9]), .d4(in_9),
    .q4(shift_register_3_q12[8]), .d5(in_10), .q5(shift_register_3_q12[7]), .d6(in_11),
    .q6(shift_register_3_q12[6]), .d7(Dato_2), .q7(shift_register_3_q12[5]), .d8(in_13),
    .q8(shift_register_3_q12[4]), .d9(in_14), .q9(shift_register_3_q12[3]), .d10(in_15),
    .q10(shift_register_3_q12[2]), .d11(in_16), .q11(shift_register_3_q12[1]), .d12(even_parity_4_out),
    .q12(shift_register_3_q12[0]));  // open: clr
  Shift_Register #(.length(13)) shift_register_4 (
    .shift(or_8_out), .in(controlled_buffer_1_out), .clk(and_4_out), .out(shift_register_4_out),
    .load(and_4_out), .d0(Receptor_4), .q0(shift_register_4_q12[12]), .d1(in_43),
    .q1(shift_register_4_q12[11]), .d2(1'b1), .q2(shift_register_4_q12[10]), .d3(1'b1),
    .q3(shift_register_4_q12[9]), .d4(in_32), .q4(shift_register_4_q12[8]), .d5(in_33),
    .q5(shift_register_4_q12[7]), .d6(Dato_4), .q6(shift_register_4_q12[6]), .d7(in_35),
    .q7(shift_register_4_q12[5]), .d8(in_36), .q8(shift_register_4_q12[4]), .d9(in_37),
    .q9(shift_register_4_q12[3]), .d10(in_38), .q10(shift_register_4_q12[2]), .d11(in_39),
    .q11(shift_register_4_q12[1]), .d12(even_parity_3_out), .q12(shift_register_4_q12[0]));  // open: clr
  Decoder #(.select(2)) decoder_3 (
    .out1(decoder_1_out2), .out2(decoder_1_out1), .out3(decoder_2_out3), .sel({in_43, Receptor_4}), .en(in_45));  // open: out0
  and and_5 (and_5_out, ~shift_register_3_q12[12], shift_register_3_q12[11], and_3_out);  // AND_Gate
  and and_6 (and_6_out, ~shift_register_4_q12[12], ~shift_register_4_q12[11], and_3_out);  // AND_Gate
  or or_5 (or_5_out, Receptor_2, ~in_21);  // OR_Gate
  or or_6 (or_6_out, or_5_out, decoder_1_out2);
  or or_7 (or_7_out, Receptor_4, in_43);
  or or_8 (or_8_out, or_7_out, decoder_1_out0);
  assign controlled_buffer_1_out = or_5_out ? shift_register_3_out : 1'bz;  // Controlled_Buffer controlled_buffer_3
  assign controlled_buffer_1_out = or_7_out ? shift_register_4_out : 1'bz;  // Controlled_Buffer controlled_buffer_4
  Decoder #(.select(2)) decoder_4 (
    .out0(decoder_1_out0), .out1(decoder_1_out1), .out3(decoder_2_out3), .sel({in_21, Receptor_2}), .en(in_23));  // open: out2
  xnor even_parity_3 (even_parity_3_out, in_32, in_33, Dato_4, in_35, in_36, in_37, in_38, in_39);
  xnor even_parity_4 (even_parity_4_out, in_9, in_10, in_11, Dato_2, in_13, in_14, in_15, in_16);
  Hex_Digit_Display hex_digit_display_9 (.value(out_47[12:9]));  // open: dp
  Register #(.width(13)) register_3 (.D(shift_register_3_q12), .Q(out_47), .clk(and_5_out));  // open: en, clr
  Hex_Digit_Display hex_digit_display_10 (.value(out_49[12:9]));  // open: dp
  Register #(.width(13)) register_4 (.D(shift_register_4_q12), .Q(out_49), .clk(and_6_out));  // open: en, clr
  Hex_Digit_Display hex_digit_display_11 (.value(out_47[8:5]));  // open: dp
  Hex_Digit_Display hex_digit_display_12 (.value(out_47[4:1]));  // open: dp
  Hex_Digit_Display hex_digit_display_13 (.value(out_49[4:1]));  // open: dp
  Hex_Digit_Display hex_digit_display_14 (.value(out_49[8:5]));  // open: dp
  Hex_Digit_Display hex_digit_display_15 (.value({3'b000, out_47[0]}));  // open: dp
  Hex_Digit_Display hex_digit_display_16 (.value({3'b000, out_49[0]}));  // open: dp

  // Notes on the sheet:
  //   Fuente
  //   Nº de registro= 11
  //   Fuente
  //   Nº de registro= 10
  //   Actualmente, el programa es capaz de enviar los bits al receptor que se seleccione, si no envía nada, el receptor será el mismo.
  //   El problema que no he conseguido solventar al pasar de 2 a 4 dispositivos es que todos activan la salida por pantalla (mal) 
  //   Pero solo el receptor recibe el mensaje correcto, los demás solo tienen el mensaje que tenían al principio de la ejecución.
  //   Fuente
  //   Nº de registro= 01
  //   Fuente
  //   Nº de registro= 00
  //   Inicio
endmodule
