// Logisim project DAAC PR2_1.circ as structural Verilog: 1 circuit, main circuit main
module main (
  input  in_1,
  input  in_2,
  input  in_3,
  input  in_4,
  input  in_5,
  input  in_6,
  input  in_7,
  input  in_8,
  input  Shift_1,
  input  in_10,
  input  Serial_IN,
  input  Start_1___0,
  output out_13,
  output out_14,
  output out_15,
  output out_16
);

  wire and_1_out, clock_1_out, not_1_out, shift_register_1_out;
  wire [3:0] shift_register_2_q3, shift_register_2_q7;

  Shift_Register shift_register_1 (
    .shift(Shift_1), .in(Serial_IN), .clk(and_1_out), .out(shift_register_1_out), .load(Start_1___0),
    .d0(in_1), .d1(in_2), .d2(in_3), .d3(in_4), .d4(in_5), .d5(in_6), .d6(in_7), .d7(in_8));  // open: clr, q0, q1, q2, q3, q4, q5, q6, q7
  Counter #(.width(4), .max('hf)) C (
    .Q({out_16, out_15, out_14, out_13}), .clk(and_1_out), .clr(Start_1___0));  // open: load, D, count, carry
  LED led_1 (.in(shift_register_1_out));
  Clock clock_1 (.out(clock_1_out));
  and and_1 (and_1_out, clock_1_out, not_1_out);
  not not_1 (not_1_out, out_16);
  Hex_Digit_Display hex_digit_display_1 (.value({out_16, out_15, out_14, out_13}));  // open: dp
  Shift_Register shift_register_2 (
    .shift(in_10), .in(shift_register_1_out), .clk(and_1_out), .q0(shift_register_2_q3[3]),
    .q1(shift_register_2_q3[2]), .q2(shift_register_2_q3[1]), .q3(shift_register_2_q3[0]),
    .q4(shift_register_2_q7[3]), .q5(shift_register_2_q7[2]), .q6(shift_register_2_q7[1]),
    .q7(shift_register_2_q7[0]));  // open: out, load, clr, d0, d1, d2, d3, d4, d5, d6, d7
  Hex_Digit_Display hex_digit_display_2 (.value(shift_register_2_q7));  // open: dp
  Hex_Digit_Display hex_digit_display_3 (.value(shift_register_2_q3));  // open: dp

  // Notes on the sheet:
  //   Contador 0->F
  //   Control cuenta 0->7
endmodule
