// Logisim project DAAC PR2_2.circ as structural Verilog: 1 circuit, main circuit main
module main (
  input  in_1,
  input  in_2,
  input  in_3,
  input  in_4,
  input  in_5,
  input  in_6,
  input  in_7,
  input  in_8,
  input  in_9,
  input  in_10,
  input  in_11,
  input  in_12,
  input  in_13
);

  wire and_1_out, and_2_out, and_3_out, clock_1_out, not_1_out, not_2_out, shift_register_1_out;
  wire [3:0] counter_1_q;
  wire [7:0] register_1_q, register_2_q, shift_register_2_q7, shift_register_3_q7;

  Shift_Register shift_register_1 (
    .shift(in_9), .in(in_11), .clk(and_1_out), .out(shift_register_1_out), .load(in_12), .d0(in_1),
    .d1(in_2), .d2(in_7), .d3(in_8), .d4(in_3), .d5(in_4), .d6(in_5), .d7(in_6));  // open: clr, q0, q1, q2, q3, q4, q5, q6, q7
  Counter #(.width(4), .max('hf)) counter_1 (
    .Q(counter_1_q), .clk(and_1_out), .clr(in_12));  // open: load, D, count, carry
  not not_1 (not_1_out, counter_1_q[3]);
  Clock clock_1 (.out(clock_1_out));
  and and_1 (and_1_out, clock_1_out, not_1_out);
  Shift_Register shift_register_2 (
    .shift(in_10), .in(shift_register_1_out), .clk(and_1_out), .q0(shift_register_2_q7[7]),
    .q1(shift_register_2_q7[6]), .q2(shift_register_2_q7[5]), .q3(shift_register_2_q7[4]),
    .q4(shift_register_2_q7[3]), .q5(shift_register_2_q7[2]), .q6(shift_register_2_q7[1]),
    .q7(shift_register_2_q7[0]));  // open: out, load, clr, d0, d1, d2, d3, d4, d5, d6, d7
  and and_2 (and_2_out, shift_register_2_q7[7], shift_register_2_q7[6]);
  Shift_Register shift_register_3 (
    .shift(in_13), .in(shift_register_1_out), .clk(and_1_out), .q0(shift_register_3_q7[7]),
    .q1(shift_register_3_q7[6]), .q2(shift_register_3_q7[5]), .q3(shift_register_3_q7[4]),
    .q4(shift_register_3_q7[3]), .q5(shift_register_3_q7[2]), .q6(shift_register_3_q7[1]),
    .q7(shift_register_3_q7[0]));  // open: out, load, clr, d0, d1, d2, d3, d4, d5, d6, d7
  not not_2 (not_2_out, shift_register_3_q7[7]);
  and and_3 (and_3_out, not_2_out, shift_register_3_q7[6]);
  Hex_Digit_Display hex_digit_display_1 (.value({2'b00, register_1_q[7:6]}));  // open: dp
  Register register_1 (.D(shift_register_2_q7), .Q(register_1_q), .clk(and_2_out));  // open: en, clr
  Register register_2 (.D(shift_register_3_q7), .Q(register_2_q), .clk(and_3_out));  // open: en, clr
  Hex_Digit_Display hex_digit_display_2 (.value(register_1_q[3:0]));  // open: dp
  Hex_Digit_Display hex_digit_display_3 (.value({2'b00, register_2_q[7:6]}));  // open: dp
  Hex_Digit_Display hex_digit_display_4 (.value(register_2_q[3:0]));  // open: dp
endmodule
