// Logisim project DAAC PR2_3.circ as structural Verilog: 1 circuit, main circuit main
module main (
  input  in_1,
  input  in_2,
  input  in_3,
  input  in_4,
  input  in_5,
  input  in_6,
  input  in_7,
  input  in_8,
  input  in_9,
  input  in_10,
  input  in_11,
  input  in_12,
  input  in_13,
  input  in_14,
  input  in_15,
  input  in_16,
  input  in_17,
  input  in_18,
  input  in_19,
  input  in_20,
  input  in_21
);

  wire and_1_out, clock_1_out, controlled_buffer_1_out, not_1_out, shift_register_1_out, shift_register_2_out;
  wire [3:0] counter_1_q;

  Shift_Register shift_register_1 (
    .shift(in_17), .in(controlled_buffer_1_out), .clk(and_1_out), .out(shift_register_1_out), .load(in_21),
    .d0(in_1), .d1(in_2), .d2(in_3), .d3(in_4), .d4(in_7), .d5(in_8), .d6(in_9), .d7(in_10));  // open: clr, q0, q1, q2, q3, q4, q5, q6, q7
  Counter #(.width(4), .max('hf)) counter_1 (
    .Q(counter_1_q), .clk(and_1_out), .clr(in_21));  // open: load, D, count, carry
  Clock clock_1 (.out(clock_1_out));
  not not_1 (not_1_out, counter_1_q[3]);
  and and_1 (and_1_out, clock_1_out, not_1_out);
  assign controlled_buffer_1_out = in_19 ? shift_register_1_out : 1'bz;  // Controlled_Buffer controlled_buffer_1
  Shift_Register shift_register_2 (
    .shift(in_18), .in(controlled_buffer_1_out), .clk(and_1_out), .out(shift_register_2_out), .load(in_21),
    .d0(in_5), .d1(in_6), .d2(in_11), .d3(in_12), .d4(in_13), .d5(in_14), .d6(in_15), .d7(in_16));  // open: clr, q0, q1, q2, q3, q4, q5, q6, q7
  assign controlled_buffer_1_out = in_20 ? shift_register_2_out : 1'bz;  // Controlled_Buffer controlled_buffer_2
endmodule
