// Logisim project DAAC PR2_4_mod.circ as structural Verilog: 1 circuit, main circuit main
module main (
  input  in_1,
  input  in_2,
  input  in_3,
  input  Dato,
  input  in_5,
  input  in_6,
  input  in_7,
  input  in_8,
  input  in_9,
  input  in_10,
  input  in_11,
  input  in_12,
  input  in_13,
  input  in_14,
  input  in_15,
  input  in_16,
  input  Inicio,
  input  Receptor,
  input  in_19,
  input  Receptor_2,
  input  in_21,
  input  Desplazamiento,
  input  Salida,
  input  Desplazamiento_2,
  input  Salida_2,
  input  in_26,
  input  in_27,
  input  in_28,
  input  in_29,
  input  in_30,
  input  in_31,
  input  in_32,
  input  in_33,
  input  in_34,
  input  in_35,
  input  in_36,
  input  in_37,
  input  in_38,
  input  in_39,
  input  in_40,
  input  in_41,
  input  Receptor_3,
  input  in_43,
  input  Receptor_4,
  input  in_45,
  input  Desplazamiento_3,
  input  Desplazamiento_4,
  input  Salida_3,
  input  Salida_4,
  output [12:0] out_50,
  output [12:0] out_51,
  output [12:0] out_52,
  output [12:0] out_53
);

  wire and_1_out, and_2_out, and_3_out, and_4_out, and_5_out, clock_1_out, even_parity_1_out,
       even_parity_2_out, even_parity_3_out, even_parity_4_out, not_1_out, shift_register_1_out,
       shift_register_2_out, shift_register_3_out, shift_register_4_out, undriven, undriven_2, undriven_3,
       undriven_4;
  wire [3:0] counter_1_q;
  wire [12:0] shift_register_1_q12, shift_register_2_q12, shift_register_3_q12, shift_register_4_q12;

  Shift_Register #(.length(13)) shift_register_1 (
    .shift(Desplazamiento), .in(undriven), .clk(and_3_out), .out(shift_register_1_out), .load(Inicio),
    .d0(Receptor), .q0(shift_register_1_q12[12]), .d1(in_19), .q1(shift_register_1_q12[11]), .d2(1'b1),
    .q2(shift_register_1_q12[10]), .d3(1'b1), .q3(shift_register_1_q12[9]), .d4(in_1),
    .q4(shift_register_1_q12[8]), .d5(in_2), .q5(shift_register_1_q12[7]), .d6(in_3),
    .q6(shift_register_1_q12[6]), .d7(Dato), .q7(shift_register_1_q12[5]), .d8(in_5),
    .q8(shift_register_1_q12[4]), .d9(in_6), .q9(shift_register_1_q12[3]), .d10(in_7),
    .q10(shift_register_1_q12[2]), .d11(in_8), .q11(shift_register_1_q12[1]), .d12(even_parity_1_out),
    .q12(shift_register_1_q12[0]));  // open: clr
  Shift_Register #(.length(13)) shift_register_2 (
    .shift(Desplazamiento_3), .in(undriven_2), .clk(and_3_out), .out(shift_register_2_out), .load(Inicio),
    .d0(Receptor_3), .q0(shift_register_2_q12[12]), .d1(in_43), .q1(shift_register_2_q12[11]), .d2(1'b1),
    .q2(shift_register_2_q12[10]), .d3(1'b0), .q3(shift_register_2_q12[9]), .d4(in_26),
    .q4(shift_register_2_q12[8]), .d5(in_27), .q5(shift_register_2_q12[7]), .d6(in_28),
    .q6(shift_register_2_q12[6]), .d7(in_29), .q7(shift_register_2_q12[5]), .d8(in_30),
    .q8(shift_register_2_q12[4]), .d9(in_31), .q9(shift_register_2_q12[3]), .d10(in_32),
    .q10(shift_register_2_q12[2]), .d11(in_33), .q11(shift_register_2_q12[1]), .d12(even_parity_2_out),
    .q12(shift_register_2_q12[0]));  // open: clr
  and and_1 (and_1_out, shift_register_1_q12[11], shift_register_1_q12[12], Salida, counter_1_q[3]);
  and and_2 (and_2_out, shift_register_2_q12[11], shift_register_2_q12[12], Salida_3, counter_1_q[3]);
  Controlled_Buffer controlled_buffer_1 (.in(shift_register_1_out), .en(Salida));  // open: out
  Controlled_Buffer controlled_buffer_2 (.in(shift_register_2_out), .en(Salida_3));  // open: out
  xnor even_parity_1 (even_parity_1_out, in_1, in_2, in_3, Dato, in_5, in_6, in_7, in_8);
  Hex_Digit_Display hex_digit_display_1 (.value(out_50[8:5]));  // open: dp
  Hex_Digit_Display hex_digit_display_2 (.value(out_50[12:9]));  // open: dp
  Register #(.width(13)) register_1 (.D(shift_register_1_q12), .Q(out_50), .clk(and_1_out));  // open: en, clr
  xnor even_parity_2 (even_parity_2_out, in_26, in_27, in_28, in_29, in_30, in_31, in_32, in_33);
  Hex_Digit_Display hex_digit_display_3 (.value(out_52[8:5]));  // open: dp
  Hex_Digit_Display hex_digit_display_4 (.value(out_52[12:9]));  // open: dp
  Register #(.width(13)) register_2 (.D(shift_register_2_q12), .Q(out_52), .clk(and_2_out));  // open: en, clr
  Hex_Digit_Display hex_digit_display_5 (.value({3'b000, out_50[0]}));  // open: dp
  Hex_Digit_Display hex_digit_display_6 (.value(out_50[4:1]));  // open: dp
  Hex_Digit_Display hex_digit_display_7 (.value({3'b000, out_52[0]}));  // open: dp
  Hex_Digit_Display hex_digit_display_8 (.value(out_52[4:1]));  // open: dp
  Counter #(.width(4), .max('hf)) counter_1 (
    .Q(counter_1_q), .clk(and_3_out), .clr(Inicio));  // open: load, D, count, carry
  Clock clock_1 (.out(clock_1_out));
  not not_1 (not_1_out, counter_1_q[3]);
  and and_3 (and_3_out, clock_1_out, not_1_out);
  Shift_Register #(.length(13)) shift_register_3 (
    .shift(Desplazamiento_4), .in(undriven_3), .clk(and_3_out), .out(shift_register_3_out), .load(Inicio),
    .d0(Receptor_4), .q0(shift_register_3_q12[12]), .d1(in_45), .q1(shift_register_3_q12[11]), .d2(1'b0),
    .q2(shift_register_3_q12[10]), .d3(1'b0), .q3(shift_register_3_q12[9]), .d4(in_34),
    .q4(shift_register_3_q12[8]), .d5(in_35), .q5(shift_register_3_q12[7]), .d6(in_36),
    .q6(shift_register_3_q12[6]), .d7(in_37), .q7(shift_register_3_q12[5]), .d8(in_38),
    .q8(shift_register_3_q12[4]), .d9(in_39), .q9(shift_register_3_q12[3]), .d10(in_40),
    .q10(shift_register_3_q12[2]), .d11(in_41), .q11(shift_register_3_q12[1]), .d12(even_parity_3_out),
    .q12(shift_register_3_q12[0]));  // open: clr
  and and_4 (and_4_out, shift_register_3_q12[11], shift_register_3_q12[12], Salida_4, counter_1_q[3]);
  Shift_Register #(.length(13)) shift_register_4 (
    .shift(Desplazamiento_2), .in(undriven_4), .clk(and_3_out), .out(shift_register_4_out), .load(Inicio),
    .d0(Receptor_2), .q0(shift_register_4_q12[12]), .d1(in_21), .q1(shift_register_4_q12[11]), .d2(1'b0),
    .q2(shift_register_4_q12[10]), .d3(1'b1), .q3(shift_register_4_q12[9]), .d4(in_9),
    .q4(shift_register_4_q12[8]), .d5(in_10), .q5(shift_register_4_q12[7]), .d6(in_11),
    .q6(shift_register_4_q12[6]), .d7(in_12), .q7(shift_register_4_q12[5]), .d8(in_13),
    .q8(shift_register_4_q12[4]), .d9(in_14), .q9(shift_register_4_q12[3]), .d10(in_15),
    .q10(shift_register_4_q12[2]), .d11(in_16), .q11(shift_register_4_q12[1]), .d12(even_parity_4_out),
    .q12(shift_register_4_q12[0]));  // open: clr
  and and_5 (and_5_out, shift_register_4_q12[11], shift_register_4_q12[12], Salida_2, counter_1_q[3]);
  Controlled_Buffer controlled_buffer_3 (.in(shift_register_3_out), .en(Salida_4));  // open: out
  Controlled_Buffer controlled_buffer_4 (.in(shift_register_4_out), .en(Salida_2));  // open: out
  xnor even_parity_3 (even_parity_3_out, in_34, in_35, in_36, in_37, in_38, in_39, in_40, in_41);
  Hex_Digit_Display hex_digit_display_9 (.value(out_53[8:5]));  // open: dp
  Hex_Digit_Display hex_digit_display_10 (.value(out_53[12:9]));  // open: dp
  Register #(.width(13)) register_3 (.D(shift_register_3_q12), .Q(out_53), .clk(and_4_out));  // open: en, clr
  xnor even_parity_4 (even_parity_4_out, in_9, in_10, in_11, in_12, in_13, in_14, in_15, in_16);
  Hex_Digit_Display hex_digit_display_11 (.value(out_51[12:9]));  // open: dp
  Register #(.width(13)) register_4 (.D(shift_register_4_q12), .Q(out_51), .clk(and_5_out));  // open: en, clr
  Hex_Digit_Display hex_digit_display_12 (.value(out_53[4:1]));  // open: dp
  Hex_Digit_Display hex_digit_display_13 (.value({3'b000, out_53[0]}));  // open: dp
  Hex_Digit_Display hex_digit_display_14 (.value(out_51[8:5]));  // open: dp
  Hex_Digit_Display hex_digit_display_15 (.value(out_51[4:1]));  // open: dp
  Hex_Digit_Display hex_digit_display_16 (.value({3'b000, out_51[0]}));  // open: dp

  // Notes on the sheet:
  //   Fuente
  //   Nº de registro= 11
  //   Fuente
  //   Nº de registro= 10
  //   Fuente
  //   Nº de registro= 00
  //   Fuente
  //   Nº de registro= 01
endmodule
