// Logisim project Arcos_Herrera_Raul_P3.circ as structural Verilog: 1 circuit, main circuit main
module main (
  input  in_1,
  input  in_2,
  input  in_3,
  input  in_4,
  input  in_5,
  input  in_6,
  input  in_7,
  input  in_8,
  input  in_9,
  input  in_10,
  input  in_11,
  input  in_12,
  input  in_13,
  input  in_14,
  input  in_15,
  input  in_16,
  input  in_17,
  input  in_18,
  input  Carga_DIR,
  input  SEL_RAM,
  input  Control,
  input  START,
  input  Direcc_IN_OUT,
  input  in_24,
  input  BUS_o_PRT_E_S,
  input  in_26,
  input  in_27,
  input  in_28,
  input  in_29,
  input  in_30,
  input  in_31,
  input  in_32,
  input  in_33,
  input  in_34,
  input  in_35,
  input  in_36,
  input  in_37,
  input  in_38,
  input  in_39,
  input  in_40,
  input  in_41,
  input  in_42,
  input  in_43,
  input  in_44,
  input  in_45,
  input  in_46,
  input  in_47,
  input  in_48,
  input  in_49,
  input  in_50,
  input  in_51,
  input  in_52,
  input  in_53,
  input  in_54,
  input  in_55,
  input  in_56,
  input  in_57,
  input  in_58,
  input  in_59,
  input  Generador_RAND,
  input  in_61,
  input  in_62,
  input  in_63,
  input  in_64,
  input  in_65,
  input  in_66,
  input  in_67,
  input  in_68,
  input  in_69,
  input  in_70,
  input  in_71,
  input  in_72,
  input  in_73,
  input  in_74,
  output [3:0] out_75,
  output [7:0] out_76,
  output out_77,
  output out_78,
  output out_79,
  output out_80,
  output out_81,
  output out_82,
  output out_83,
  output out_84,
  output out_85,
  output out_86,
  output out_87,
  output out_88,
  output out_89,
  output out_90,
  output out_91,
  output out_92,
  output out_93,
  output out_94,
  output out_95,
  output out_96,
  output out_97,
  output out_98,
  output out_99,
  output out_100,
  output out_101,
  output out_102,
  output out_103,
  output out_104,
  output out_105,
  output out_106,
  output out_107,
  output out_108
);

  wire and_1_out, and_2_out, and_3_out, and_4_out, and_5_out, and_6_out, and_7_out, and_8_out, and_9_out,
       and_10_out, and_11_out, clock_1_out, clock_2_out, clock_3_out, clock_4_out, clock_5_out,
       counter_1_carry, demultiplexer_1_out0, demultiplexer_1_out1, demultiplexer_1_out2,
       demultiplexer_1_out5, not_1_out, not_2_out, not_3_out, not_4_out, not_5_out, not_6_out, not_7_out;
  wire [7:0] controlled_buffer_6_out, controlled_buffer_7_out, controlled_buffer_8_out,
       controlled_buffer_9_out, controlled_buffer_10_out, multiplexer_1_out, multiplexer_2_out,
       multiplexer_3_out, multiplexer_4_out, random_1_out, random_2_out, random_3_out, random_4_out,
       register_1_q, register_3_q, register_5_q, register_7_q;

  Clock clock_1 (.out(clock_1_out));
  Counter #(.width(4), .max('hf)) counter_1 (
    .load(Carga_DIR), .D({in_12, in_13, in_14, in_15}), .count(Control), .Q(out_75), .carry(counter_1_carry),
    .clk(and_1_out), .clr(START));
  not not_1 (not_1_out, counter_1_carry);
  and and_1 (and_1_out, clock_1_out, not_1_out);
  Demultiplexer #(.select(3)) demultiplexer_1 (
    .out0(demultiplexer_1_out0), .out1(demultiplexer_1_out1), .out2(demultiplexer_1_out2),
    .out5(demultiplexer_1_out5), .in(BUS_o_PRT_E_S), .sel({in_33, in_30, in_28}), .en(1'b1));  // open: out3, out4, out6, out7
  RAM #(.addrWidth(4)) ram_1 (
    .addr(out_75), .data(out_76), .sel(SEL_RAM), .clk(clock_1_out), .ld(Direcc_IN_OUT));  // open: clr
  not not_2 (not_2_out, BUS_o_PRT_E_S);
  and and_2 (and_2_out, demultiplexer_1_out5, not_3_out);
  not not_3 (not_3_out, Direcc_IN_OUT);
  and and_3 (and_3_out, Direcc_IN_OUT, demultiplexer_1_out5);
  assign out_76 = and_2_out ? controlled_buffer_6_out : 8'bz;  // Controlled_Buffer controlled_buffer_1
  and and_4 (and_4_out, not_2_out, not_4_out);
  not not_4 (not_4_out, Direcc_IN_OUT);
  and and_5 (and_5_out, Direcc_IN_OUT, not_2_out);
  assign out_76 = and_4_out ? controlled_buffer_7_out : 8'bz;  // Controlled_Buffer controlled_buffer_2
  and and_6 (and_6_out, demultiplexer_1_out2, not_5_out);
  not not_5 (not_5_out, Direcc_IN_OUT);
  and and_7 (and_7_out, Direcc_IN_OUT, demultiplexer_1_out2);
  assign out_76 = and_6_out ? controlled_buffer_8_out : 8'bz;  // Controlled_Buffer controlled_buffer_3
  and and_8 (and_8_out, demultiplexer_1_out1, not_6_out);
  not not_6 (not_6_out, Direcc_IN_OUT);
  and and_9 (and_9_out, Direcc_IN_OUT, demultiplexer_1_out1);
  assign out_76 = and_8_out ? controlled_buffer_9_out : 8'bz;  // Controlled_Buffer controlled_buffer_4
  and and_10 (and_10_out, demultiplexer_1_out0, not_7_out);
  not not_7 (not_7_out, Direcc_IN_OUT);
  and and_11 (and_11_out, Direcc_IN_OUT, demultiplexer_1_out0);
  assign out_76 = and_10_out ? controlled_buffer_10_out : 8'bz;  // Controlled_Buffer controlled_buffer_5
  assign controlled_buffer_6_out = and_3_out ? out_76 : 8'bz;  // Controlled_Buffer controlled_buffer_6
  assign controlled_buffer_7_out = and_5_out ? out_76 : 8'bz;  // Controlled_Buffer controlled_buffer_7
  assign controlled_buffer_8_out = and_7_out ? out_76 : 8'bz;  // Controlled_Buffer controlled_buffer_8
  assign controlled_buffer_9_out = and_9_out ? out_76 : 8'bz;  // Controlled_Buffer controlled_buffer_9
  assign controlled_buffer_10_out = and_11_out ? out_76 : 8'bz;  // Controlled_Buffer controlled_buffer_10
  Hex_Digit_Display hex_digit_display_1 (.value(controlled_buffer_6_out[7:4]), .dp(in_8));
  Hex_Digit_Display hex_digit_display_2 (.value(controlled_buffer_7_out[7:4]), .dp(in_26));
  Hex_Digit_Display hex_digit_display_3 (.value(controlled_buffer_7_out[3:0]), .dp(in_26));
  Hex_Digit_Display hex_digit_display_4 (.value(controlled_buffer_8_out[7:4]), .dp(in_37));
  Clock clock_2 (.out(clock_2_out));
  Random random_1 (.clk(clock_2_out), .next(in_45), .out(random_1_out), .clr(in_46));
  Hex_Digit_Display hex_digit_display_5 (.value(controlled_buffer_9_out[7:4]), .dp(in_52));
  Hex_Digit_Display hex_digit_display_6 (.value(controlled_buffer_10_out[7:4]), .dp(in_67));
  Hex_Digit_Display hex_digit_display_7 (.value(controlled_buffer_6_out[3:0]), .dp(in_8));
  Hex_Digit_Display hex_digit_display_8 (.value(controlled_buffer_8_out[3:0]), .dp(in_37));
  Hex_Digit_Display hex_digit_display_9 (.value(controlled_buffer_9_out[3:0]), .dp(in_52));
  Clock clock_3 (.out(clock_3_out));
  Random random_2 (.clk(clock_3_out), .next(Generador_RAND), .out(random_2_out), .clr(in_61));
  Hex_Digit_Display hex_digit_display_10 (.value(controlled_buffer_10_out[3:0]), .dp(in_67));
  Multiplexer #(.width(8)) multiplexer_1 (
    .in0(random_3_out), .in1({in_18, in_11, in_10, in_9, in_6, in_5, in_4, in_3}), .out(multiplexer_1_out),
    .sel(in_7), .en(1'b1));
  Register register_1 (.D(multiplexer_1_out), .Q(register_1_q), .clk(in_16));  // open: en, clr
  assign controlled_buffer_6_out = in_17 ? register_1_q : 8'bz;  // Controlled_Buffer controlled_buffer_11
  Register register_2 (
    .D(controlled_buffer_6_out), .Q({out_84, out_83, out_82, out_81, out_80, out_79, out_78, out_77}),
    .clk(in_24));  // open: en, clr
  Multiplexer #(.width(8)) multiplexer_2 (
    .in0(random_4_out), .in1({in_43, in_40, in_39, in_38, in_36, in_34, in_32, in_31}),
    .out(multiplexer_2_out), .sel(in_35), .en(1'b1));
  Register register_3 (.D(multiplexer_2_out), .Q(register_3_q), .clk(in_41));  // open: en, clr
  assign controlled_buffer_8_out = in_42 ? register_3_q : 8'bz;  // Controlled_Buffer controlled_buffer_12
  Register register_4 (
    .D(controlled_buffer_8_out), .Q({out_92, out_91, out_90, out_89, out_88, out_87, out_86, out_85}),
    .clk(in_44));  // open: en, clr
  Multiplexer #(.width(8)) multiplexer_3 (
    .in0(random_1_out), .in1({in_58, in_55, in_54, in_53, in_51, in_50, in_48, in_47}),
    .out(multiplexer_3_out), .sel(in_49), .en(1'b1));
  assign controlled_buffer_9_out = in_57 ? register_5_q : 8'bz;  // Controlled_Buffer controlled_buffer_13
  Register register_5 (.D(multiplexer_3_out), .Q(register_5_q), .clk(in_56));  // open: en, clr
  Register register_6 (
    .D(controlled_buffer_9_out), .Q({out_100, out_99, out_98, out_97, out_96, out_95, out_94, out_93}),
    .clk(in_59));  // open: en, clr
  Multiplexer #(.width(8)) multiplexer_4 (
    .in0(random_2_out), .in1({in_73, in_70, in_69, in_68, in_66, in_65, in_63, in_62}),
    .out(multiplexer_4_out), .sel(in_64), .en(1'b1));
  Register register_7 (.D(multiplexer_4_out), .Q(register_7_q), .clk(in_71));  // open: en, clr
  assign controlled_buffer_10_out = in_72 ? register_7_q : 8'bz;  // Controlled_Buffer controlled_buffer_14
  Register register_8 (
    .D(controlled_buffer_10_out),
    .Q({out_108, out_107, out_106, out_105, out_104, out_103, out_102, out_101}), .clk(in_74));  // open: en, clr
  Clock clock_4 (.out(clock_4_out));
  Random random_3 (.clk(clock_4_out), .next(in_1), .out(random_3_out), .clr(in_2));
  Clock clock_5 (.out(clock_5_out));
  Random random_4 (.clk(clock_5_out), .next(in_27), .out(random_4_out), .clr(in_29));

  // Notes on the sheet:
  //   Seleccionar entre 0, 1 , 3 , 5
  //   Dirección directa
  //   Memoria RAM - Buffer
  //   Dato 5
  //   Dato 3
  //   Dato 1
  //   Datos en bus de datos
  //   Datos en bus de datos
  //   Generador RAND
  //   Datos en bus de datos
  //   Dato 0
  //   Datos en bus de datos
  //   Bus de de E/S
  //   Datos del bus del sistema
  //   Datos del bus de E/S
  //   Datos del bus de E/S
  //   Bus de de E/S
  //   Bus de de E/S
  //   Bus de de E/S
  //   Datos del bus de E/S
  //   Generador RAND
  //   Generador RAND
endmodule
