// Logisim project DAAC PR3_1.circ as structural Verilog: 1 circuit, main circuit main
module main (
  input  in_1,
  input  in_2,
  input  in_3,
  input  in_4,
  input  in_5,
  input  in_6,
  input  in_7,
  input  Datos_de_entrada,
  input  in_9,
  input  in_10,
  input  in_11,
  input  in_12,
  input  in_13,
  input  R_W,
  input  in_15,
  input  CS,
  input  OE,
  input  CLEAR,
  output out_19,
  output out_20,
  output out_21,
  output out_22,
  output out_23,
  output out_24,
  output out_25,
  output out_26
);

  wire not_1_out;
  wire [7:0] controlled_buffer_1_out;

  assign controlled_buffer_1_out = not_1_out ? {in_1, in_2, in_3, in_4, in_5, in_6, in_7, Datos_de_entrada} : 8'bz;  // Controlled_Buffer controlled_buffer_1
  assign {out_26, out_25, out_24, out_23, out_22, out_21, out_20, out_19} = OE ? controlled_buffer_1_out : 8'bz;  // Controlled_Buffer controlled_buffer_2
  RAM #(.addrWidth(4)) ram_1 (
    .addr({in_13, in_12, in_10, in_9}), .data(controlled_buffer_1_out), .sel(CS), .clk(R_W), .ld(OE),
    .clr(CLEAR));
  not not_1 (not_1_out, OE);
  Hex_Digit_Display hex_digit_display_1 (.value({in_5, in_6, in_7, Datos_de_entrada}), .dp(in_11));
  Hex_Digit_Display hex_digit_display_2 (.value({in_1, in_2, in_3, in_4}), .dp(in_11));
  Hex_Digit_Display hex_digit_display_3 (.value({out_26, out_25, out_24, out_23}), .dp(in_15));
  Hex_Digit_Display hex_digit_display_4 (.value({out_22, out_21, out_20, out_19}), .dp(in_15));

  // Notes on the sheet:
  //   Bus de direcciones
  //   Datos de salida
endmodule
