// Logisim project DAAC PR3_2.circ as structural Verilog: 1 circuit, main circuit main
module main (
  input  in_1,
  input  in_2,
  input  in_3,
  input  in_4,
  input  in_5,
  input  in_6,
  input  in_7,
  input  Datos_de_entrada,
  input  in_9,
  input  in_10,
  input  in_11,
  input  in_12,
  input  in_13,
  input  CS,
  input  CLEAR,
  input  R_W,
  input  OE,
  input  in_18,
  input  in_19,
  input  Selecctor,
  input  [4:0] Puerto,
  input  in_22,
  output out_23,
  output out_24,
  output out_25,
  output out_26,
  output out_27,
  output out_28,
  output out_29,
  output out_30,
  output out_31,
  output out_32
);

  wire not_1_out;
  wire [3:0] ram_1_data, ram_1_data_2;
  wire [7:0] controlled_buffer_2_out, register_1_q;

  Decoder #(.select(5), .disabled(0)) decoder_1 (
    .out26(out_31), .out30(out_32), .sel(Puerto), .en(Selecctor));  // open: out0, out1, out2, out3, out4, out5, out6, out7, out8, out9, out10, out11, out12, out13, out14, out15, out16, out17, out18, out19, out20, out21, out22, out23, out24, out25, out27, out28, out29, out31
  Hex_Digit_Display hex_digit_display_1 (.value(ram_1_data_2), .dp(in_18));
  Hex_Digit_Display hex_digit_display_2 (.value(Puerto[3:0]), .dp(in_22));
  Hex_Digit_Display hex_digit_display_3 (.value({3'b000, Puerto[4]}), .dp(in_22));
  RAM #(.addrWidth(4)) ram_1 (
    .addr({in_1, in_2, in_3, in_4}), .data({ram_1_data_2, ram_1_data}), .sel(CS), .clk(R_W), .ld(OE),
    .clr(CLEAR));
  Hex_Digit_Display hex_digit_display_4 (.value(ram_1_data), .dp(in_18));
  assign {ram_1_data_2, ram_1_data} = not_1_out ? register_1_q : 8'bz;  // Controlled_Buffer controlled_buffer_1
  not not_1 (not_1_out, OE);
  assign controlled_buffer_2_out = OE ? {ram_1_data_2, ram_1_data} : 8'bz;  // Controlled_Buffer controlled_buffer_2
  Hex_Digit_Display hex_digit_display_5 (.value({in_5, in_6, in_7, Datos_de_entrada}), .dp(in_13));
  Register register_1 (
    .D({in_5, in_6, in_7, Datos_de_entrada, in_9, in_10, in_11, in_12}), .Q(register_1_q), .clk(out_32));  // open: en, clr
  Hex_Digit_Display hex_digit_display_6 (.value({in_9, in_10, in_11, in_12}), .dp(in_13));
  Register register_2 (
    .D(controlled_buffer_2_out), .Q({out_30, out_29, out_28, out_27, out_26, out_25, out_24, out_23}),
    .clk(out_31));  // open: en, clr
  Hex_Digit_Display hex_digit_display_7 (.value({out_30, out_29, out_28, out_27}), .dp(in_19));
  Hex_Digit_Display hex_digit_display_8 (.value({out_26, out_25, out_24, out_23}), .dp(in_19));

  // Notes on the sheet:
  //   Bus de direcciones
  //   Puerto 1B
  //   Puerto 1E
  //   Nº de Puerto de E/S
  //   Bus de datos (dato)
  //   Puerto de entrada 0x1E
  //   Puerto de Salida 0x1B
  //   Datos de salida
endmodule
