// Logisim project DAAC PR3_3.circ as structural Verilog: 1 circuit, main circuit main
module main (
  input  in_1,
  input  in_2,
  input  in_3,
  input  in_4,
  input  in_5,
  input  in_6,
  input  in_7,
  input  in_8,
  input  in_9,
  input  in_10,
  input  in_11,
  input  in_12,
  input  in_13,
  input  in_14,
  input  in_15,
  input  Carga_DIR,
  input  SEL_RAM,
  input  Control,
  input  START,
  input  Direcc_IN_OUT,
  input  in_21,
  input  BUS_o_PRT_E_S,
  input  in_23,
  output [3:0] out_24,
  output [7:0] out_25,
  output out_26,
  output out_27,
  output out_28,
  output out_29,
  output out_30,
  output out_31,
  output out_32,
  output out_33
);

  wire and_1_out, and_2_out, and_3_out, and_4_out, and_5_out, clock_1_out, counter_1_carry, not_1_out,
       not_2_out, not_3_out, not_4_out;
  wire [7:0] controlled_buffer_3_out, controlled_buffer_4_out, register_1_q;

  Clock clock_1 (.out(clock_1_out));
  Counter #(.width(4), .max('hf)) counter_1 (
    .load(Carga_DIR), .D({in_9, in_10, in_11, in_12}), .count(Control), .Q(out_24), .carry(counter_1_carry),
    .clk(and_1_out), .clr(START));
  not not_1 (not_1_out, counter_1_carry);
  and and_1 (and_1_out, clock_1_out, not_1_out);
  RAM #(.addrWidth(4)) ram_1 (
    .addr(out_24), .data(out_25), .sel(SEL_RAM), .clk(clock_1_out), .ld(Direcc_IN_OUT));  // open: clr
  not not_2 (not_2_out, BUS_o_PRT_E_S);
  and and_2 (and_2_out, BUS_o_PRT_E_S, not_3_out);
  not not_3 (not_3_out, Direcc_IN_OUT);
  and and_3 (and_3_out, Direcc_IN_OUT, BUS_o_PRT_E_S);
  assign out_25 = and_2_out ? controlled_buffer_3_out : 8'bz;  // Controlled_Buffer controlled_buffer_1
  and and_4 (and_4_out, not_2_out, not_4_out);
  not not_4 (not_4_out, Direcc_IN_OUT);
  and and_5 (and_5_out, Direcc_IN_OUT, not_2_out);
  assign out_25 = and_4_out ? controlled_buffer_4_out : 8'bz;  // Controlled_Buffer controlled_buffer_2
  assign controlled_buffer_3_out = and_3_out ? out_25 : 8'bz;  // Controlled_Buffer controlled_buffer_3
  assign controlled_buffer_4_out = and_5_out ? out_25 : 8'bz;  // Controlled_Buffer controlled_buffer_4
  Hex_Digit_Display hex_digit_display_1 (.value(controlled_buffer_3_out[7:4]), .dp(in_5));
  Hex_Digit_Display hex_digit_display_2 (.value(controlled_buffer_4_out[3:0]), .dp(in_23));
  Hex_Digit_Display hex_digit_display_3 (.value(controlled_buffer_4_out[7:4]), .dp(in_23));
  Hex_Digit_Display hex_digit_display_4 (.value(controlled_buffer_3_out[3:0]), .dp(in_5));
  assign controlled_buffer_3_out = in_14 ? register_1_q : 8'bz;  // Controlled_Buffer controlled_buffer_5
  Register register_1 (
    .D({in_15, in_8, in_7, in_6, in_4, in_3, in_2, in_1}), .Q(register_1_q), .clk(in_13));  // open: en, clr
  Register register_2 (
    .D(controlled_buffer_3_out), .Q({out_33, out_32, out_31, out_30, out_29, out_28, out_27, out_26}),
    .clk(in_21));  // open: en, clr

  // Notes on the sheet:
  //   Dirección directa
  //   Memoria RAM - Buffer
  //   Datos en bus de datos
  //   Bus de de E/S
  //   Datos del bus del sistema
  //   Datos del bus de E/S
  //   Bus de datos del sistema
endmodule
