// Logisim project Arcos_Herrera_Raul_P4.circ as structural Verilog: 1 circuit, main circuit main
module main (
  input  in_1,
  input  in_2,
  input  in_3,
  input  in_4,
  input  Carga_DIR__0,
  input  SEL_RAM,
  input  Control__1,
  input  W0_R1,
  input  START__0__1,
  input  BUS_0__o_E_S__1,
  input  in_11,
  input  in_12,
  input  Indice_Puntero,
  input  in_14,
  input  in_15,
  input  in_16,
  input  in_17,
  input  SEL_RAM_2,
  input  Salida_Activa,
  input  SEL_RAM_3,
  input  in_21,
  input  in_22,
  input  in_23,
  input  in_24,
  input  in_25,
  input  in_26,
  input  in_27,
  input  in_28,
  input  in_29,
  input  in_30,
  input  in_31,
  input  in_32,
  output [3:0] out_33,
  output [7:0] out_34,
  output out_35,
  output out_36,
  output out_37,
  output out_38,
  output out_39,
  output out_40,
  output out_41,
  output out_42,
  output out_43,
  output out_44,
  output out_45,
  output out_46,
  output out_47,
  output out_48,
  output out_49,
  output out_50,
  output out_51,
  output out_52,
  output out_53,
  output out_54,
  output out_55,
  output out_56,
  output out_57,
  output out_58,
  output out_59,
  output out_60,
  output out_61,
  output out_62,
  output out_63,
  output out_64,
  output out_65,
  output out_66,
  output out_67,
  output out_68,
  output out_69,
  output out_70,
  output out_71,
  output out_72,
  output out_73,
  output out_74
);

  wire and_1_out, and_2_out, and_3_out, and_4_out, and_5_out, and_6_out, and_7_out, and_8_out, and_9_out,
       and_10_out, and_11_out, and_12_out, and_13_out, counter_2_carry, demultiplexer_1_out0,
       demultiplexer_1_out1, demultiplexer_1_out2, demultiplexer_1_out5, F, F_2, F_4, F_8, F_16, not_1_out,
       not_2_out, not_3_out, not_4_out, not_5_out, not_6_out, not_7_out, not_8_out, not_9_out;
  wire [3:0] ram_3_data, ram_3_data_2;
  wire [7:0] controlled_buffer_5_out, controlled_buffer_7_out, controlled_buffer_8_out,
       controlled_buffer_9_out, controlled_buffer_11_out, random_1_out, random_2_out, random_3_out,
       random_4_out, random_5_out, register_1_q, register_3_q, register_5_q, register_7_q, register_9_q;
  wire [7:4] counter_1_q;
  wire [11:0] ram_1_data;

  Clock clock_1 (.out(F));
  Counter counter_1 (.Q({counter_1_q, F_16, F_8, F_4, F_2}), .clk(F));  // open: load, D, count, carry, clr
  Counter #(.width(4), .max('hf)) counter_2 (
    .load(Carga_DIR__0), .count(Control__1), .Q(out_33), .carry(counter_2_carry), .clk(and_1_out),
    .clr(START__0__1));  // open: D
  not not_1 (not_1_out, counter_2_carry);
  and and_1 (and_1_out, F_8, not_1_out);
  Hex_Digit_Display hex_digit_display_1 (.value(ram_1_data[11:8]));  // open: dp
  RAM #(.addrWidth(3), .dataWidth(12)) ram_1 (
    .addr({Indice_Puntero, in_14, in_15}), .data(ram_1_data), .sel(SEL_RAM_2), .ld(Salida_Activa));  // open: clk, clr
  Hex_Digit_Display hex_digit_display_2 (.value(ram_1_data[3:0]));  // open: dp
  Hex_Digit_Display hex_digit_display_3 (.value(ram_1_data[7:4]));  // open: dp
  RAM #(.addrWidth(4)) ram_2 (.addr(out_33), .data(out_34), .sel(SEL_RAM), .clk(F_8), .ld(W0_R1));  // open: clr
  Hex_Digit_Display hex_digit_display_4 (.value(out_33));  // open: dp
  not not_2 (not_2_out, W0_R1);
  RAM #(.addrWidth(16)) ram_3 (
    .addr({ram_1_data, out_33}), .data({ram_3_data_2, ram_3_data}), .sel(SEL_RAM_3), .clk(F_8), .ld(not_2_out));  // open: clr
  Hex_Digit_Display hex_digit_display_5 (.value(out_34[7:4]), .dp(in_2));
  Hex_Digit_Display hex_digit_display_6 (.value(out_34[3:0]), .dp(in_2));
  Demultiplexer #(.select(3)) demultiplexer_1 (
    .out0(demultiplexer_1_out0), .out1(demultiplexer_1_out1), .out2(demultiplexer_1_out2),
    .out5(demultiplexer_1_out5), .in(BUS_0__o_E_S__1), .sel({in_23, in_22, in_21}), .en(1'b1));  // open: out3, out4, out6, out7
  not not_3 (not_3_out, BUS_0__o_E_S__1);
  and and_2 (and_2_out, BUS_0__o_E_S__1, not_4_out);
  not not_4 (not_4_out, W0_R1);
  and and_3 (and_3_out, W0_R1, BUS_0__o_E_S__1);
  assign out_34 = and_2_out ? controlled_buffer_5_out : 8'bz;  // Controlled_Buffer controlled_buffer_1
  and and_4 (and_4_out, not_3_out, not_5_out);
  not not_5 (not_5_out, W0_R1);
  and and_5 (and_5_out, W0_R1, not_3_out);
  assign out_34 = and_4_out ? {ram_3_data_2, ram_3_data} : 8'bz;  // Controlled_Buffer controlled_buffer_2
  and and_6 (and_6_out, demultiplexer_1_out5, not_6_out);
  not not_6 (not_6_out, W0_R1);
  and and_7 (and_7_out, W0_R1, demultiplexer_1_out5);
  assign out_34 = and_6_out ? controlled_buffer_7_out : 8'bz;  // Controlled_Buffer controlled_buffer_3
  and and_8 (and_8_out, demultiplexer_1_out2, not_7_out);
  not not_7 (not_7_out, W0_R1);
  and and_9 (and_9_out, W0_R1, demultiplexer_1_out2);
  assign out_34 = and_8_out ? controlled_buffer_8_out : 8'bz;  // Controlled_Buffer controlled_buffer_4
  not not_8 (not_8_out, W0_R1);
  not not_9 (not_9_out, W0_R1);
  assign controlled_buffer_5_out = and_3_out ? out_34 : 8'bz;  // Controlled_Buffer controlled_buffer_5
  Hex_Digit_Display hex_digit_display_7 (.value(controlled_buffer_5_out[7:4]), .dp(in_3));
  assign {ram_3_data_2, ram_3_data} = and_5_out ? out_34 : 8'bz;  // Controlled_Buffer controlled_buffer_6
  Hex_Digit_Display hex_digit_display_8 (.value(ram_3_data_2), .dp(in_11));
  assign controlled_buffer_7_out = and_7_out ? out_34 : 8'bz;  // Controlled_Buffer controlled_buffer_7
  Hex_Digit_Display hex_digit_display_9 (.value(controlled_buffer_7_out[7:4]), .dp(in_16));
  assign controlled_buffer_8_out = and_9_out ? out_34 : 8'bz;  // Controlled_Buffer controlled_buffer_8
  Hex_Digit_Display hex_digit_display_10 (.value(controlled_buffer_8_out[7:4]), .dp(in_25));
  assign controlled_buffer_9_out = and_11_out ? out_34 : 8'bz;  // Controlled_Buffer controlled_buffer_9
  and and_10 (and_10_out, demultiplexer_1_out1, not_8_out);
  and and_11 (and_11_out, W0_R1, demultiplexer_1_out1);
  assign out_34 = and_10_out ? controlled_buffer_9_out : 8'bz;  // Controlled_Buffer controlled_buffer_10
  assign controlled_buffer_11_out = and_13_out ? out_34 : 8'bz;  // Controlled_Buffer controlled_buffer_11
  and and_12 (and_12_out, demultiplexer_1_out0, not_9_out);
  and and_13 (and_13_out, W0_R1, demultiplexer_1_out0);
  assign out_34 = and_12_out ? controlled_buffer_11_out : 8'bz;  // Controlled_Buffer controlled_buffer_12
  Hex_Digit_Display hex_digit_display_11 (.value(controlled_buffer_5_out[3:0]), .dp(in_3));
  Hex_Digit_Display hex_digit_display_12 (.value(ram_3_data), .dp(in_11));
  Hex_Digit_Display hex_digit_display_13 (.value(controlled_buffer_7_out[3:0]), .dp(in_16));
  Hex_Digit_Display hex_digit_display_14 (.value(controlled_buffer_8_out[3:0]), .dp(in_25));
  Hex_Digit_Display hex_digit_display_15 (.value(controlled_buffer_9_out[3:0]), .dp(in_28));
  Hex_Digit_Display hex_digit_display_16 (.value(controlled_buffer_9_out[7:4]), .dp(in_28));
  Hex_Digit_Display hex_digit_display_17 (.value(controlled_buffer_11_out[3:0]), .dp(in_31));
  Hex_Digit_Display hex_digit_display_18 (.value(controlled_buffer_11_out[7:4]), .dp(in_31));
  Register register_1 (.D(random_1_out), .Q(register_1_q), .clk(and_1_out));  // open: en, clr
  Register register_2 (
    .D(controlled_buffer_5_out), .Q({out_42, out_41, out_40, out_39, out_38, out_37, out_36, out_35}),
    .clk(F_8));  // open: en, clr
  Register register_3 (.D(random_2_out), .Q(register_3_q), .clk(F));  // open: en, clr
  Register register_4 (
    .D(controlled_buffer_7_out), .Q({out_50, out_49, out_48, out_47, out_46, out_45, out_44, out_43}),
    .clk(F_8));  // open: en, clr
  Register register_5 (.D(random_3_out), .Q(register_5_q), .clk(F));  // open: en, clr
  Register register_6 (
    .D(controlled_buffer_8_out), .Q({out_58, out_57, out_56, out_55, out_54, out_53, out_52, out_51}),
    .clk(F_8));  // open: en, clr
  assign controlled_buffer_5_out = in_1 ? register_1_q : 8'bz;  // Controlled_Buffer controlled_buffer_13
  Hex_Digit_Display hex_digit_display_19 (.value({out_42, out_41, out_40, out_39}), .dp(in_4));
  assign controlled_buffer_7_out = in_12 ? register_3_q : 8'bz;  // Controlled_Buffer controlled_buffer_14
  assign controlled_buffer_8_out = in_24 ? register_5_q : 8'bz;  // Controlled_Buffer controlled_buffer_15
  assign controlled_buffer_9_out = in_27 ? register_7_q : 8'bz;  // Controlled_Buffer controlled_buffer_16
  Register register_7 (.D(random_4_out), .Q(register_7_q), .clk(F));  // open: en, clr
  Register register_8 (
    .D(controlled_buffer_9_out), .Q({out_66, out_65, out_64, out_63, out_62, out_61, out_60, out_59}),
    .clk(F_8));  // open: en, clr
  Register register_9 (.D(random_5_out), .Q(register_9_q), .clk(F));  // open: en, clr
  assign controlled_buffer_11_out = in_30 ? register_9_q : 8'bz;  // Controlled_Buffer controlled_buffer_17
  Register register_10 (
    .D(controlled_buffer_11_out), .Q({out_74, out_73, out_72, out_71, out_70, out_69, out_68, out_67}),
    .clk(F_8));  // open: en, clr
  Random random_1 (.clk(F), .next(1'b1), .out(random_1_out));  // open: clr
  Hex_Digit_Display hex_digit_display_20 (.value({out_38, out_37, out_36, out_35}), .dp(in_4));
  Random random_2 (.clk(F), .next(1'b1), .out(random_2_out));  // open: clr
  Hex_Digit_Display hex_digit_display_21 (.value({out_46, out_45, out_44, out_43}), .dp(in_17));
  Hex_Digit_Display hex_digit_display_22 (.value({out_50, out_49, out_48, out_47}), .dp(in_17));
  Random random_3 (.clk(F), .next(1'b1), .out(random_3_out));  // open: clr
  Hex_Digit_Display hex_digit_display_23 (.value({out_58, out_57, out_56, out_55}), .dp(in_26));
  Hex_Digit_Display hex_digit_display_24 (.value({out_54, out_53, out_52, out_51}), .dp(in_26));
  Random random_4 (.clk(F), .next(1'b1), .out(random_4_out));  // open: clr
  Hex_Digit_Display hex_digit_display_25 (.value({out_62, out_61, out_60, out_59}), .dp(in_29));
  Hex_Digit_Display hex_digit_display_26 (.value({out_66, out_65, out_64, out_63}), .dp(in_29));
  Random random_5 (.clk(F), .next(1'b1), .out(random_5_out));  // open: clr
  Hex_Digit_Display hex_digit_display_27 (.value({out_74, out_73, out_72, out_71}), .dp(in_32));
  Hex_Digit_Display hex_digit_display_28 (.value({out_70, out_69, out_68, out_67}), .dp(in_32));

  // Notes on the sheet:
  //   Generador de reloj con división a 4 frecuencias 
  //   Tabla de Punteros E/S
  //   Memoria RAM - Buffer
  //   Dir de Memoria del Sistema
  //   W1/R0
  //   Memoria Ram del Sistema 64Kx8
  //   Datos entrada/salida Buffer
  //   Selector entre 0,1,3,5
  //   Bus de datos del sistema
  //   Datos en bus de datos
  //   Bus de de E/S
  //   Bus de de E/S
  //   Bus de de E/S
  //   Bus de de E/S
  //   Bus de de E/S
  //   Datos del bus de E/S
  //   Datos del bus del sistema
  //   Datos del bus de E/S
  //   Datos del bus de E/S
  //   Datos del bus de E/S
  //   Datos del bus de E/S
  //   Numeros aleatorios de entrada
  //   Numeros aleatorios de entrada
  //   Numeros aleatorios de entrada
  //   Numeros aleatorios de entrada
  //   Numeros aleatorios de entrada
  //   Datos puerto de salida
endmodule
