// Logisim project DAAC PR4_Inicio.circ as structural Verilog: 1 circuit, main circuit main
module main (
  input  in_1,
  input  in_2,
  input  in_3,
  input  in_4,
  input  Carga_DIR__0,
  input  SEL_RAM,
  input  Control__1,
  input  W0_R1,
  input  START__0__1,
  input  BUS_0__o_E_S__1,
  input  in_11,
  input  Indice_Puntero,
  input  in_13,
  input  in_14,
  input  SEL_RAM_2,
  input  Salida_Activa,
  input  SEL_RAM_3,
  output [3:0] out_18,
  output [7:0] out_19,
  output out_20,
  output out_21,
  output out_22,
  output out_23,
  output out_24,
  output out_25,
  output out_26,
  output out_27
);

  wire and_1_out, and_2_out, and_3_out, and_4_out, and_5_out, counter_1_carry, F, F_2, F_4, F_8, F_16,
       not_1_out, not_2_out, not_3_out, not_4_out, not_5_out;
  wire [3:0] ram_3_data, ram_3_data_2;
  wire [7:0] controlled_buffer_3_out, random_1_out, register_1_q;
  wire [7:4] counter_2_q;
  wire [11:0] ram_1_data;

  Counter #(.width(4), .max('hf)) counter_1 (
    .load(Carga_DIR__0), .count(Control__1), .Q(out_18), .carry(counter_1_carry), .clk(and_1_out),
    .clr(START__0__1));  // open: D
  not not_1 (not_1_out, counter_1_carry);
  and and_1 (and_1_out, F_8, not_1_out);
  Hex_Digit_Display hex_digit_display_1 (.value(ram_1_data[11:8]));  // open: dp
  RAM #(.addrWidth(3), .dataWidth(12)) ram_1 (
    .addr({Indice_Puntero, in_13, in_14}), .data(ram_1_data), .sel(SEL_RAM_2), .ld(Salida_Activa));  // open: clk, clr
  Hex_Digit_Display hex_digit_display_2 (.value(ram_1_data[7:4]));  // open: dp
  Hex_Digit_Display hex_digit_display_3 (.value(ram_1_data[3:0]));  // open: dp
  RAM #(.addrWidth(4)) ram_2 (.addr(out_18), .data(out_19), .sel(SEL_RAM), .clk(F_8), .ld(W0_R1));  // open: clr
  Hex_Digit_Display hex_digit_display_4 (.value(out_18));  // open: dp
  not not_2 (not_2_out, W0_R1);
  RAM #(.addrWidth(16)) ram_3 (
    .addr({ram_1_data, out_18}), .data({ram_3_data_2, ram_3_data}), .sel(SEL_RAM_3), .clk(F_8), .ld(not_2_out));  // open: clr
  Hex_Digit_Display hex_digit_display_5 (.value(out_19[7:4]), .dp(in_2));
  Hex_Digit_Display hex_digit_display_6 (.value(out_19[3:0]), .dp(in_2));
  not not_3 (not_3_out, BUS_0__o_E_S__1);
  and and_2 (and_2_out, BUS_0__o_E_S__1, not_4_out);
  not not_4 (not_4_out, W0_R1);
  and and_3 (and_3_out, W0_R1, BUS_0__o_E_S__1);
  assign out_19 = and_2_out ? controlled_buffer_3_out : 8'bz;  // Controlled_Buffer controlled_buffer_1
  and and_4 (and_4_out, not_3_out, not_5_out);
  not not_5 (not_5_out, W0_R1);
  and and_5 (and_5_out, W0_R1, not_3_out);
  assign out_19 = and_4_out ? {ram_3_data_2, ram_3_data} : 8'bz;  // Controlled_Buffer controlled_buffer_2
  assign controlled_buffer_3_out = and_3_out ? out_19 : 8'bz;  // Controlled_Buffer controlled_buffer_3
  Hex_Digit_Display hex_digit_display_7 (.value(controlled_buffer_3_out[7:4]), .dp(in_3));
  assign {ram_3_data_2, ram_3_data} = and_5_out ? out_19 : 8'bz;  // Controlled_Buffer controlled_buffer_4
  Hex_Digit_Display hex_digit_display_8 (.value(ram_3_data_2), .dp(in_11));
  Hex_Digit_Display hex_digit_display_9 (.value(controlled_buffer_3_out[3:0]), .dp(in_3));
  Hex_Digit_Display hex_digit_display_10 (.value(ram_3_data), .dp(in_11));
  Register register_1 (.D(random_1_out), .Q(register_1_q), .clk(and_1_out));  // open: en, clr
  Register register_2 (
    .D(controlled_buffer_3_out), .Q({out_27, out_26, out_25, out_24, out_23, out_22, out_21, out_20}),
    .clk(F_8));  // open: en, clr
  Clock clock_1 (.out(F));
  Counter counter_2 (.Q({counter_2_q, F_16, F_8, F_4, F_2}), .clk(F));  // open: load, D, count, carry, clr
  assign controlled_buffer_3_out = in_1 ? register_1_q : 8'bz;  // Controlled_Buffer controlled_buffer_5
  Hex_Digit_Display hex_digit_display_11 (.value({out_27, out_26, out_25, out_24}), .dp(in_4));
  Random random_1 (.clk(F), .next(1'b1), .out(random_1_out));  // open: clr
  Hex_Digit_Display hex_digit_display_12 (.value({out_23, out_22, out_21, out_20}), .dp(in_4));

  // Notes on the sheet:
  //   Tabla de Punteros E/S
  //   Memoria RAM - Buffer
  //   Dir de Memoria del Sistema
  //   W1/R0
  //   Memoria Ram del Sistema 64Kx8
  //   Datos entrada/salida Buffer
  //   Bus de datos del sistema
  //   Datos en bus de datos
  //   Bus de de E/S
  //   Datos del bus de E/S
  //   Datos del bus del sistema
  //   Generador de reloj con división a 4 frecuencias 
  //   Numeros aleatorios de entrada
  //   Datos puerto de salida
endmodule
