// Logisim project DAAC P56 _SPI.circ as structural Verilog: 1 circuit, main circuit main
module main (
  input  [1:0] SSX
);

  wire CLK, MOSI0, MOSI1, MOSI2, MOSI3, multiplexer_1_out, not_1_out, not_2_out, not_3_out, RESET, SS1, SS2,
       SS3;
  wire [1:0] register_1_q;
  wire [7:0] counter_1_q, DSE1, DSE2, DSE3, random_1_out, random_2_out, random_3_out, random_4_out,
       register_2_q, shift_register_1_q7, shift_register_2_q7, shift_register_3_q7, shift_register_4_q7;

  Clock clock_1 (.out(CLK));
  Counter counter_1 (.Q(counter_1_q), .clk(CLK), .clr(RESET));  // open: load, D, count, carry
  Multiplexer #(.select(2)) multiplexer_1 (
    .in1(MOSI1), .in2(MOSI2), .in3(MOSI3), .out(multiplexer_1_out), .sel(register_1_q));  // open: in0, en
  Demultiplexer #(.select(2)) demultiplexer_1 (
    .out1(SS1), .out2(SS2), .out3(SS3), .in(counter_1_q[3]), .sel(register_1_q));  // open: out0, en
  Register #(.width(2)) register_1 (.D(SSX), .Q(register_1_q), .clk(counter_1_q[3]), .clr(RESET));  // open: en
  nor nor_1 (RESET, SSX[0], SSX[1]);
  Random random_1 (.clk(counter_1_q[3]), .out(random_1_out));  // open: next, clr
  Shift_Register shift_register_1 (
    .shift(1'b1), .in(multiplexer_1_out), .clk(CLK), .out(MOSI0), .load(counter_1_q[3]), .clr(RESET),
    .d0(random_1_out[7]), .q0(shift_register_1_q7[7]), .d1(random_1_out[6]), .q1(shift_register_1_q7[6]),
    .d2(random_1_out[5]), .q2(shift_register_1_q7[5]), .d3(random_1_out[4]), .q3(shift_register_1_q7[4]),
    .d4(random_1_out[3]), .q4(shift_register_1_q7[3]), .d5(random_1_out[2]), .q5(shift_register_1_q7[2]),
    .d6(random_1_out[1]), .q6(shift_register_1_q7[1]), .d7(random_1_out[0]), .q7(shift_register_1_q7[0]));
  Register register_2 (.D(shift_register_1_q7), .Q(register_2_q), .clk(counter_1_q[3]));  // open: en, clr
  Hex_Digit_Display hex_digit_display_1 (.value(register_2_q[7:4]));  // open: dp
  Hex_Digit_Display hex_digit_display_2 (.value(register_2_q[3:0]));  // open: dp
  Hex_Digit_Display hex_digit_display_3 (.value(DSE1[7:4]));  // open: dp
  Hex_Digit_Display hex_digit_display_4 (.value(DSE1[3:0]));  // open: dp
  not not_1 (not_1_out, SS1);
  Hex_Digit_Display hex_digit_display_5 (.value(DSE2[7:4]));  // open: dp
  Random random_2 (.clk(not_1_out), .out(random_2_out));  // open: next, clr
  Shift_Register shift_register_2 (
    .shift(not_1_out), .in(MOSI0), .clk(CLK), .out(MOSI1), .load(SS1), .clr(RESET), .d0(random_2_out[7]),
    .q0(shift_register_2_q7[7]), .d1(random_2_out[6]), .q1(shift_register_2_q7[6]), .d2(random_2_out[5]),
    .q2(shift_register_2_q7[5]), .d3(random_2_out[4]), .q3(shift_register_2_q7[4]), .d4(random_2_out[3]),
    .q4(shift_register_2_q7[3]), .d5(random_2_out[2]), .q5(shift_register_2_q7[2]), .d6(random_2_out[1]),
    .q6(shift_register_2_q7[1]), .d7(random_2_out[0]), .q7(shift_register_2_q7[0]));
  Random random_3 (.clk(not_2_out), .out(random_3_out));  // open: next, clr
  Shift_Register shift_register_3 (
    .shift(not_2_out), .in(MOSI0), .clk(CLK), .out(MOSI2), .load(SS2), .clr(RESET), .d0(random_3_out[7]),
    .q0(shift_register_3_q7[7]), .d1(random_3_out[6]), .q1(shift_register_3_q7[6]), .d2(random_3_out[5]),
    .q2(shift_register_3_q7[5]), .d3(random_3_out[4]), .q3(shift_register_3_q7[4]), .d4(random_3_out[3]),
    .q4(shift_register_3_q7[3]), .d5(random_3_out[2]), .q5(shift_register_3_q7[2]), .d6(random_3_out[1]),
    .q6(shift_register_3_q7[1]), .d7(random_3_out[0]), .q7(shift_register_3_q7[0]));
  not not_2 (not_2_out, SS2);
  Random random_4 (.clk(not_3_out), .out(random_4_out));  // open: next, clr
  Shift_Register shift_register_4 (
    .shift(not_3_out), .in(MOSI0), .clk(CLK), .out(MOSI3), .load(SS3), .clr(RESET), .d0(random_4_out[7]),
    .q0(shift_register_4_q7[7]), .d1(random_4_out[6]), .q1(shift_register_4_q7[6]), .d2(random_4_out[5]),
    .q2(shift_register_4_q7[5]), .d3(random_4_out[4]), .q3(shift_register_4_q7[4]), .d4(random_4_out[3]),
    .q4(shift_register_4_q7[3]), .d5(random_4_out[2]), .q5(shift_register_4_q7[2]), .d6(random_4_out[1]),
    .q6(shift_register_4_q7[1]), .d7(random_4_out[0]), .q7(shift_register_4_q7[0]));
  not not_3 (not_3_out, SS3);
  Hex_Digit_Display hex_digit_display_6 (.value(DSE2[3:0]));  // open: dp
  Hex_Digit_Display hex_digit_display_7 (.value(DSE3[7:4]));  // open: dp
  Register register_3 (.D(shift_register_2_q7), .Q(DSE1), .clk(SS1));  // open: en, clr
  Register register_4 (.D(shift_register_3_q7), .Q(DSE2), .clk(SS2));  // open: en, clr
  Register register_5 (.D(shift_register_4_q7), .Q(DSE3), .clk(SS3));  // open: en, clr
  Hex_Digit_Display hex_digit_display_8 (.value(DSE3[3:0]));  // open: dp

  // Notes on the sheet:
  //   SSX
  //   MISO
  //   Al seleccionar al Maestro
  //   Dato almacenado Maesto
  //   Dato almacenado  Esc. 01
  //   Dato almacenado  Esc 02
  //   SS1
  //   SS2
  //   SS3
  //   Dato almacenado  Esc. 03
endmodule
