// Logisim project Arcos_Herrera_Raul_P6.circ as structural Verilog: 1 circuit, main circuit main
module main (
  input  [6:0] SSX,
  input  in_2,
  input  in_3,
  input  in_4,
  input  in_5,
  input  Carga_DIR__0,
  input  SEL_RAM,
  input  Control__1,
  input  W0_R1,
  input  START__0__1,
  input  BUS_0__o_E_S__1,
  input  in_12,
  input  in_13,
  input  Indice_Puntero,
  input  in_15,
  input  in_16,
  input  in_17,
  input  in_18,
  input  SEL_RAM_2,
  input  Salida_Activa,
  input  SEL_RAM_3,
  input  in_22,
  input  in_23,
  input  in_24,
  input  in_25,
  input  in_26,
  input  in_27,
  input  in_28,
  input  in_29,
  input  in_30,
  input  in_31,
  input  in_32,
  input  in_33,
  output [3:0] out_34,
  output [7:0] out_35,
  output out_36,
  output out_37,
  output out_38,
  output out_39,
  output out_40,
  output out_41,
  output out_42,
  output out_43,
  output out_44,
  output out_45,
  output out_46,
  output out_47,
  output out_48,
  output out_49,
  output out_50,
  output out_51,
  output out_52,
  output out_53,
  output out_54,
  output out_55,
  output out_56,
  output out_57,
  output out_58,
  output out_59,
  output out_60,
  output out_61,
  output out_62,
  output out_63,
  output out_64,
  output out_65,
  output out_66,
  output out_67,
  output out_68,
  output out_69,
  output out_70,
  output out_71,
  output out_72,
  output out_73,
  output out_74,
  output out_75
);

  wire and_1_out, and_2_out, and_3_out, and_4_out, and_5_out, and_6_out, and_7_out, and_8_out, and_9_out,
       and_10_out, and_11_out, and_12_out, and_13_out, CLK, counter_2_carry, demultiplexer_2_out0,
       demultiplexer_2_out1, demultiplexer_2_out2, demultiplexer_2_out5, F, F_2, F_4, F_8, F_16, MOSI0,
       MOSI1, MOSI2, MOSI3, MOSI4, MOSI5, MOSI6, MOSI7, multiplexer_1_out, not_1_out, not_2_out, not_3_out,
       not_4_out, not_5_out, not_6_out, not_7_out, not_8_out, not_9_out, not_10_out, not_11_out, not_12_out,
       not_13_out, not_14_out, not_15_out, not_16_out, RESET, SS1, SS2, SS3, SS4, SS5, SS6, SS7;
  wire [2:0] register_1_q;
  wire [3:0] ram_3_data, ram_3_data_2;
  wire [7:0] controlled_buffer_1_out, controlled_buffer_9_out, controlled_buffer_10_out,
       controlled_buffer_11_out, controlled_buffer_12_out, controlled_buffer_13_out, counter_3_q, DSE1, DSE2,
       DSE3, DSE4, DSE5, DSE6, DSE7, random_1_out, random_2_out, random_3_out, random_4_out, random_5_out,
       random_6_out, random_7_out, random_8_out, random_9_out, random_10_out, random_11_out, random_12_out,
       register_5_q, register_7_q, register_9_q, register_13_q, register_14_q, shift_register_1_q7,
       shift_register_2_q7, shift_register_3_q7, shift_register_4_q7, shift_register_5_q7,
       shift_register_6_q7, shift_register_7_q7, shift_register_8_q7;
  wire [7:4] counter_1_q;
  wire [11:0] ram_1_data;

  Counter counter_1 (.Q({counter_1_q, F_16, F_8, F_4, F_2}), .clk(F));  // open: load, D, count, carry, clr
  Clock clock_1 (.out(F));
  assign controlled_buffer_1_out = SSX[3] ? out_35 : 8'bz;  // Controlled_Buffer controlled_buffer_1
  Clock clock_2 (.out(CLK));
  Counter #(.width(4), .max('hf)) counter_2 (
    .load(Carga_DIR__0), .count(Control__1), .Q(out_34), .carry(counter_2_carry), .clk(and_1_out),
    .clr(START__0__1));  // open: D
  and and_1 (and_1_out, F_8, not_1_out);
  RAM #(.addrWidth(3), .dataWidth(12)) ram_1 (
    .addr({Indice_Puntero, in_15, in_16}), .data(ram_1_data), .sel(SEL_RAM_2), .ld(Salida_Activa));  // open: clk, clr
  Counter counter_3 (.Q(counter_3_q), .clk(CLK), .clr(RESET));  // open: load, D, count, carry
  not not_1 (not_1_out, counter_2_carry);
  Hex_Digit_Display hex_digit_display_1 (.value(ram_1_data[11:8]));  // open: dp
  Demultiplexer #(.select(3)) demultiplexer_1 (
    .out0(SS1), .out1(SS2), .out2(SS3), .out3(SS4), .out4(SS5), .out5(SS6), .out6(SS7), .in(counter_3_q[3]),
    .sel(register_1_q));  // open: out7, en
  Hex_Digit_Display hex_digit_display_2 (.value(ram_1_data[7:4]));  // open: dp
  Hex_Digit_Display hex_digit_display_3 (.value(ram_1_data[3:0]));  // open: dp
  Multiplexer #(.select(3)) multiplexer_1 (
    .in0(MOSI1), .in1(MOSI2), .in2(MOSI3), .in3(MOSI4), .in4(MOSI5), .in5(MOSI6), .in6(MOSI7),
    .out(multiplexer_1_out), .sel(register_1_q));  // open: in7, en
  Register #(.width(3)) register_1 (.D(SSX[2:0]), .Q(register_1_q), .clk(counter_3_q[3]), .clr(RESET));  // open: en
  nor nor_1 (RESET, SSX[0], SSX[1], SSX[2]);
  Hex_Digit_Display hex_digit_display_4 (.value(out_35[7:4]), .dp(in_3));
  RAM #(.addrWidth(4)) ram_2 (.addr(out_34), .data(out_35), .sel(SEL_RAM), .clk(F_8), .ld(W0_R1));  // open: clr
  Hex_Digit_Display hex_digit_display_5 (.value(out_34));  // open: dp
  not not_2 (not_2_out, W0_R1);
  RAM #(.addrWidth(16)) ram_3 (
    .addr({ram_1_data, out_34}), .data({ram_3_data_2, ram_3_data}), .sel(SEL_RAM_3), .clk(F_8), .ld(not_2_out));  // open: clr
  Shift_Register shift_register_1 (
    .shift(1'b1), .in(multiplexer_1_out), .clk(CLK), .out(MOSI0), .load(counter_3_q[3]), .clr(RESET),
    .d0(out_35[7]), .q0(shift_register_1_q7[7]), .d1(out_35[6]), .q1(shift_register_1_q7[6]), .d2(out_35[5]),
    .q2(shift_register_1_q7[5]), .d3(out_35[4]), .q3(shift_register_1_q7[4]), .d4(out_35[3]),
    .q4(shift_register_1_q7[3]), .d5(out_35[2]), .q5(shift_register_1_q7[2]), .d6(out_35[1]),
    .q6(shift_register_1_q7[1]), .d7(out_35[0]), .q7(shift_register_1_q7[0]));
  Hex_Digit_Display hex_digit_display_6 (.value(out_35[3:0]), .dp(in_3));
  Demultiplexer #(.select(3)) demultiplexer_2 (
    .out0(demultiplexer_2_out0), .out1(demultiplexer_2_out1), .out2(demultiplexer_2_out2),
    .out5(demultiplexer_2_out5), .in(BUS_0__o_E_S__1), .sel({in_24, in_23, in_22}), .en(1'b1));  // open: out3, out4, out6, out7
  not not_3 (not_3_out, BUS_0__o_E_S__1);
  Register register_2 (.D(shift_register_1_q7), .Q(controlled_buffer_1_out), .clk(counter_3_q[3]));  // open: en, clr
  Hex_Digit_Display hex_digit_display_7 (.value(controlled_buffer_1_out[7:4]));  // open: dp
  not not_4 (not_4_out, W0_R1);
  not not_5 (not_5_out, W0_R1);
  not not_6 (not_6_out, W0_R1);
  not not_7 (not_7_out, W0_R1);
  Hex_Digit_Display hex_digit_display_8 (.value(controlled_buffer_1_out[3:0]));  // open: dp
  not not_8 (not_8_out, SS4);
  not not_9 (not_9_out, SS5);
  and and_2 (and_2_out, BUS_0__o_E_S__1, not_4_out);
  and and_3 (and_3_out, W0_R1, BUS_0__o_E_S__1);
  assign out_35 = and_2_out ? controlled_buffer_9_out : 8'bz;  // Controlled_Buffer controlled_buffer_2
  assign {ram_3_data_2, ram_3_data} = and_5_out ? out_35 : 8'bz;  // Controlled_Buffer controlled_buffer_3
  and and_4 (and_4_out, not_3_out, not_5_out);
  and and_5 (and_5_out, W0_R1, not_3_out);
  assign out_35 = and_4_out ? {ram_3_data_2, ram_3_data} : 8'bz;  // Controlled_Buffer controlled_buffer_4
  and and_6 (and_6_out, demultiplexer_2_out5, not_6_out);
  and and_7 (and_7_out, W0_R1, demultiplexer_2_out5);
  assign out_35 = and_6_out ? controlled_buffer_10_out : 8'bz;  // Controlled_Buffer controlled_buffer_5
  and and_8 (and_8_out, demultiplexer_2_out2, not_7_out);
  and and_9 (and_9_out, W0_R1, demultiplexer_2_out2);
  assign out_35 = and_8_out ? controlled_buffer_11_out : 8'bz;  // Controlled_Buffer controlled_buffer_6
  and and_10 (and_10_out, demultiplexer_2_out1, not_10_out);
  not not_10 (not_10_out, W0_R1);
  and and_11 (and_11_out, W0_R1, demultiplexer_2_out1);
  assign out_35 = and_10_out ? controlled_buffer_12_out : 8'bz;  // Controlled_Buffer controlled_buffer_7
  and and_12 (and_12_out, demultiplexer_2_out0, not_11_out);
  not not_11 (not_11_out, W0_R1);
  and and_13 (and_13_out, W0_R1, demultiplexer_2_out0);
  assign out_35 = and_12_out ? controlled_buffer_13_out : 8'bz;  // Controlled_Buffer controlled_buffer_8
  Random random_1 (.clk(not_8_out), .out(random_1_out));  // open: next, clr
  Shift_Register shift_register_2 (
    .shift(not_8_out), .in(MOSI0), .clk(CLK), .out(MOSI4), .load(SS4), .clr(RESET), .d0(random_1_out[7]),
    .q0(shift_register_2_q7[7]), .d1(random_1_out[6]), .q1(shift_register_2_q7[6]), .d2(random_1_out[5]),
    .q2(shift_register_2_q7[5]), .d3(random_1_out[4]), .q3(shift_register_2_q7[4]), .d4(random_1_out[3]),
    .q4(shift_register_2_q7[3]), .d5(random_1_out[2]), .q5(shift_register_2_q7[2]), .d6(random_1_out[1]),
    .q6(shift_register_2_q7[1]), .d7(random_1_out[0]), .q7(shift_register_2_q7[0]));
  Random random_2 (.clk(not_9_out), .out(random_2_out));  // open: next, clr
  Shift_Register shift_register_3 (
    .shift(not_9_out), .in(MOSI0), .clk(CLK), .out(MOSI5), .load(SS5), .clr(RESET), .d0(random_2_out[7]),
    .q0(shift_register_3_q7[7]), .d1(random_2_out[6]), .q1(shift_register_3_q7[6]), .d2(random_2_out[5]),
    .q2(shift_register_3_q7[5]), .d3(random_2_out[4]), .q3(shift_register_3_q7[4]), .d4(random_2_out[3]),
    .q4(shift_register_3_q7[3]), .d5(random_2_out[2]), .q5(shift_register_3_q7[2]), .d6(random_2_out[1]),
    .q6(shift_register_3_q7[1]), .d7(random_2_out[0]), .q7(shift_register_3_q7[0]));
  assign controlled_buffer_9_out = and_3_out ? out_35 : 8'bz;  // Controlled_Buffer controlled_buffer_9
  Hex_Digit_Display hex_digit_display_9 (.value(controlled_buffer_9_out[7:4]), .dp(in_4));
  Hex_Digit_Display hex_digit_display_10 (.value(ram_3_data_2), .dp(in_12));
  assign controlled_buffer_10_out = and_7_out ? out_35 : 8'bz;  // Controlled_Buffer controlled_buffer_10
  Hex_Digit_Display hex_digit_display_11 (.value(controlled_buffer_10_out[7:4]), .dp(in_17));
  assign controlled_buffer_11_out = and_9_out ? out_35 : 8'bz;  // Controlled_Buffer controlled_buffer_11
  Hex_Digit_Display hex_digit_display_12 (.value(controlled_buffer_11_out[7:4]), .dp(in_26));
  assign controlled_buffer_12_out = and_11_out ? out_35 : 8'bz;  // Controlled_Buffer controlled_buffer_12
  assign controlled_buffer_13_out = and_13_out ? out_35 : 8'bz;  // Controlled_Buffer controlled_buffer_13
  Hex_Digit_Display hex_digit_display_13 (.value(controlled_buffer_9_out[3:0]), .dp(in_4));
  Hex_Digit_Display hex_digit_display_14 (.value(ram_3_data), .dp(in_12));
  Hex_Digit_Display hex_digit_display_15 (.value(controlled_buffer_10_out[3:0]), .dp(in_17));
  Hex_Digit_Display hex_digit_display_16 (.value(controlled_buffer_11_out[3:0]), .dp(in_26));
  Hex_Digit_Display hex_digit_display_17 (.value(controlled_buffer_12_out[3:0]), .dp(in_29));
  Hex_Digit_Display hex_digit_display_18 (.value(controlled_buffer_12_out[7:4]), .dp(in_29));
  Hex_Digit_Display hex_digit_display_19 (.value(controlled_buffer_13_out[3:0]), .dp(in_32));
  Hex_Digit_Display hex_digit_display_20 (.value(controlled_buffer_13_out[7:4]), .dp(in_32));
  Hex_Digit_Display hex_digit_display_21 (.value(DSE1[7:4]));  // open: dp
  Register register_3 (.D(shift_register_2_q7), .Q(DSE4), .clk(SS4));  // open: en, clr
  Register register_4 (.D(shift_register_3_q7), .Q(DSE5), .clk(SS5));  // open: en, clr
  Register register_5 (.D(random_6_out), .Q(register_5_q), .clk(and_1_out));  // open: en, clr
  Register register_6 (
    .D(controlled_buffer_9_out), .Q({out_43, out_42, out_41, out_40, out_39, out_38, out_37, out_36}),
    .clk(F_8));  // open: en, clr
  Register register_7 (.D(random_7_out), .Q(register_7_q), .clk(F));  // open: en, clr
  Register register_8 (
    .D(controlled_buffer_10_out), .Q({out_51, out_50, out_49, out_48, out_47, out_46, out_45, out_44}),
    .clk(F_8));  // open: en, clr
  Register register_9 (.D(random_8_out), .Q(register_9_q), .clk(F));  // open: en, clr
  Register register_10 (
    .D(controlled_buffer_11_out), .Q({out_59, out_58, out_57, out_56, out_55, out_54, out_53, out_52}),
    .clk(F_8));  // open: en, clr
  Register register_11 (
    .D(controlled_buffer_12_out), .Q({out_67, out_66, out_65, out_64, out_63, out_62, out_61, out_60}),
    .clk(F_8));  // open: en, clr
  Register register_12 (
    .D(controlled_buffer_13_out), .Q({out_75, out_74, out_73, out_72, out_71, out_70, out_69, out_68}),
    .clk(F_8));  // open: en, clr
  Hex_Digit_Display hex_digit_display_22 (.value(DSE1[3:0]));  // open: dp
  not not_12 (not_12_out, SS1);
  assign controlled_buffer_9_out = in_2 ? register_5_q : 8'bz;  // Controlled_Buffer controlled_buffer_14
  Hex_Digit_Display hex_digit_display_23 (.value({out_43, out_42, out_41, out_40}), .dp(in_5));
  assign controlled_buffer_10_out = in_13 ? register_7_q : 8'bz;  // Controlled_Buffer controlled_buffer_15
  Hex_Digit_Display hex_digit_display_24 (.value({out_51, out_50, out_49, out_48}), .dp(in_18));
  assign controlled_buffer_11_out = in_25 ? register_9_q : 8'bz;  // Controlled_Buffer controlled_buffer_16
  Hex_Digit_Display hex_digit_display_25 (.value({out_59, out_58, out_57, out_56}), .dp(in_27));
  Register register_13 (.D(random_9_out), .Q(register_13_q), .clk(F));  // open: en, clr
  assign controlled_buffer_12_out = in_28 ? register_13_q : 8'bz;  // Controlled_Buffer controlled_buffer_17
  Register register_14 (.D(random_10_out), .Q(register_14_q), .clk(F));  // open: en, clr
  assign controlled_buffer_13_out = in_31 ? register_14_q : 8'bz;  // Controlled_Buffer controlled_buffer_18
  Hex_Digit_Display hex_digit_display_26 (.value(DSE2[7:4]));  // open: dp
  Random random_3 (.clk(not_12_out), .out(random_3_out));  // open: next, clr
  Shift_Register shift_register_4 (
    .shift(not_12_out), .in(MOSI0), .clk(CLK), .out(MOSI1), .load(SS1), .clr(RESET), .d0(random_3_out[7]),
    .q0(shift_register_4_q7[7]), .d1(random_3_out[6]), .q1(shift_register_4_q7[6]), .d2(random_3_out[5]),
    .q2(shift_register_4_q7[5]), .d3(random_3_out[4]), .q3(shift_register_4_q7[4]), .d4(random_3_out[3]),
    .q4(shift_register_4_q7[3]), .d5(random_3_out[2]), .q5(shift_register_4_q7[2]), .d6(random_3_out[1]),
    .q6(shift_register_4_q7[1]), .d7(random_3_out[0]), .q7(shift_register_4_q7[0]));
  Random random_4 (.clk(not_13_out), .out(random_4_out));  // open: next, clr
  Shift_Register shift_register_5 (
    .shift(not_13_out), .in(MOSI0), .clk(CLK), .out(MOSI2), .load(SS2), .clr(RESET), .d0(random_4_out[7]),
    .q0(shift_register_5_q7[7]), .d1(random_4_out[6]), .q1(shift_register_5_q7[6]), .d2(random_4_out[5]),
    .q2(shift_register_5_q7[5]), .d3(random_4_out[4]), .q3(shift_register_5_q7[4]), .d4(random_4_out[3]),
    .q4(shift_register_5_q7[3]), .d5(random_4_out[2]), .q5(shift_register_5_q7[2]), .d6(random_4_out[1]),
    .q6(shift_register_5_q7[1]), .d7(random_4_out[0]), .q7(shift_register_5_q7[0]));
  not not_13 (not_13_out, SS2);
  Random random_5 (.clk(not_14_out), .out(random_5_out));  // open: next, clr
  Shift_Register shift_register_6 (
    .shift(not_14_out), .in(MOSI0), .clk(CLK), .out(MOSI3), .load(SS3), .clr(RESET), .d0(random_5_out[7]),
    .q0(shift_register_6_q7[7]), .d1(random_5_out[6]), .q1(shift_register_6_q7[6]), .d2(random_5_out[5]),
    .q2(shift_register_6_q7[5]), .d3(random_5_out[4]), .q3(shift_register_6_q7[4]), .d4(random_5_out[3]),
    .q4(shift_register_6_q7[3]), .d5(random_5_out[2]), .q5(shift_register_6_q7[2]), .d6(random_5_out[1]),
    .q6(shift_register_6_q7[1]), .d7(random_5_out[0]), .q7(shift_register_6_q7[0]));
  not not_14 (not_14_out, SS3);
  Random random_6 (.clk(F), .next(1'b1), .out(random_6_out));  // open: clr
  Hex_Digit_Display hex_digit_display_27 (.value({out_39, out_38, out_37, out_36}), .dp(in_5));
  Random random_7 (.clk(F), .next(1'b1), .out(random_7_out));  // open: clr
  Hex_Digit_Display hex_digit_display_28 (.value({out_47, out_46, out_45, out_44}), .dp(in_18));
  Random random_8 (.clk(F), .next(1'b1), .out(random_8_out));  // open: clr
  Hex_Digit_Display hex_digit_display_29 (.value({out_55, out_54, out_53, out_52}), .dp(in_27));
  Random random_9 (.clk(F), .next(1'b1), .out(random_9_out));  // open: clr
  Hex_Digit_Display hex_digit_display_30 (.value({out_67, out_66, out_65, out_64}), .dp(in_30));
  Hex_Digit_Display hex_digit_display_31 (.value({out_63, out_62, out_61, out_60}), .dp(in_30));
  Random random_10 (.clk(F), .next(1'b1), .out(random_10_out));  // open: clr
  Hex_Digit_Display hex_digit_display_32 (.value({out_71, out_70, out_69, out_68}), .dp(in_33));
  Hex_Digit_Display hex_digit_display_33 (.value({out_75, out_74, out_73, out_72}), .dp(in_33));
  Hex_Digit_Display hex_digit_display_34 (.value(DSE2[3:0]));  // open: dp
  Hex_Digit_Display hex_digit_display_35 (.value(DSE3[7:4]));  // open: dp
  Register register_15 (.D(shift_register_4_q7), .Q(DSE1), .clk(SS1));  // open: en, clr
  Register register_16 (.D(shift_register_5_q7), .Q(DSE2), .clk(SS2));  // open: en, clr
  Register register_17 (.D(shift_register_6_q7), .Q(DSE3), .clk(SS3));  // open: en, clr
  Hex_Digit_Display hex_digit_display_36 (.value(DSE3[3:0]));  // open: dp
  not not_15 (not_15_out, SS6);
  Random random_11 (.clk(not_15_out), .out(random_11_out));  // open: next, clr
  Shift_Register shift_register_7 (
    .shift(not_15_out), .in(MOSI0), .clk(CLK), .out(MOSI6), .load(SS6), .clr(RESET), .d0(random_11_out[7]),
    .q0(shift_register_7_q7[7]), .d1(random_11_out[6]), .q1(shift_register_7_q7[6]), .d2(random_11_out[5]),
    .q2(shift_register_7_q7[5]), .d3(random_11_out[4]), .q3(shift_register_7_q7[4]), .d4(random_11_out[3]),
    .q4(shift_register_7_q7[3]), .d5(random_11_out[2]), .q5(shift_register_7_q7[2]), .d6(random_11_out[1]),
    .q6(shift_register_7_q7[1]), .d7(random_11_out[0]), .q7(shift_register_7_q7[0]));
  Random random_12 (.clk(not_16_out), .out(random_12_out));  // open: next, clr
  Shift_Register shift_register_8 (
    .shift(not_16_out), .in(MOSI0), .clk(CLK), .out(MOSI7), .load(SS7), .clr(RESET), .d0(random_12_out[7]),
    .q0(shift_register_8_q7[7]), .d1(random_12_out[6]), .q1(shift_register_8_q7[6]), .d2(random_12_out[5]),
    .q2(shift_register_8_q7[5]), .d3(random_12_out[4]), .q3(shift_register_8_q7[4]), .d4(random_12_out[3]),
    .q4(shift_register_8_q7[3]), .d5(random_12_out[2]), .q5(shift_register_8_q7[2]), .d6(random_12_out[1]),
    .q6(shift_register_8_q7[1]), .d7(random_12_out[0]), .q7(shift_register_8_q7[0]));
  not not_16 (not_16_out, SS7);
  Hex_Digit_Display hex_digit_display_37 (.value(DSE4[3:0]));  // open: dp
  Hex_Digit_Display hex_digit_display_38 (.value(DSE4[7:4]));  // open: dp
  Register register_18 (.D(shift_register_7_q7), .Q(DSE6), .clk(SS6));  // open: en, clr
  Register register_19 (.D(shift_register_8_q7), .Q(DSE7), .clk(SS7));  // open: en, clr
  Hex_Digit_Display hex_digit_display_39 (.value(DSE5[3:0]));  // open: dp
  Hex_Digit_Display hex_digit_display_40 (.value(DSE5[7:4]));  // open: dp
  Hex_Digit_Display hex_digit_display_41 (.value(DSE6[7:4]));  // open: dp
  Hex_Digit_Display hex_digit_display_42 (.value(DSE7[7:4]));  // open: dp
  Hex_Digit_Display hex_digit_display_43 (.value(DSE6[3:0]));  // open: dp
  Hex_Digit_Display hex_digit_display_44 (.value(DSE7[3:0]));  // open: dp

  // Notes on the sheet:
  //   Generador de reloj con división a 4 frecuencias 
  //   Tabla de Punteros E/S
  //   SSX
  //   Memoria RAM - Buffer
  //   Dir de Memoria del Sistema
  //   MISO
  //   W1/R0
  //   Memoria Ram del Sistema 64Kx8
  //   Al seleccionar al Maestro
  //   Datos entrada/salida Buffer
  //   Selector entre 0,1,3,5
  //   Datos en bus de datos
  //   Bus de datos del sistema
  //   Dato almacenado Maesto
  //   Bus de de E/S
  //   Bus de de E/S
  //   Bus de de E/S
  //   SS1
  //   SS1
  //   Bus de de E/S
  //   Bus de de E/S
  //   Datos del bus de E/S
  //   Datos del bus del sistema
  //   Datos del bus de E/S
  //   Datos del bus de E/S
  //   Datos del bus de E/S
  //   Datos del bus de E/S
  //   Dato almacenado  Esc. 01
  //   Numeros aleatorios de entrada
  //   Numeros aleatorios de entrada
  //   Numeros aleatorios de entrada
  //   Numeros aleatorios de entrada
  //   Numeros aleatorios de entrada
  //   Dato almacenado  Esc 02
  //   SS1
  //   Datos puerto de salida
  //   SS2
  //   SS3
  //   Dato almacenado  Esc. 03
  //   SS1
  //   SS1
  //   Dato almacenado  Esc. 04
  //   Dato almacenado  Esc 05
  //   Dato almacenado  Esc. 06
  //   Dato almacenado  Esc. 07
endmodule
